// Digital circuit Décodeur 2 - 4.dig as structural Verilog
module \Décodeur_2____4  (
  input  a,
  input  b,
  output e0,
  output e1,
  output e2,
  output e3
);

  wire not_1_out, not_2_out;

  not not_1 (not_1_out, a);
  not not_2 (not_2_out, b);
  and and_1 (e0, not_1_out, not_2_out);
  and and_2 (e1, not_1_out, b);
  and and_3 (e2, a, not_2_out);
  and and_4 (e3, a, b);
endmodule
