// Digital circuit Décodeur 3 -> 8.dig as structural Verilog
module \Décodeur_3____8  (
  input  c,
  input  b,
  input  a,
  output s0,
  output s1,
  output s2,
  output s3,
  output s4,
  output s6,
  output s7,
  output s8
);

  wire and_1_out, and_2_out, and_3_out, and_4_out, and_5_out, and_6_out, and_7_out, and_8_out, not_1_out,
       not_2_out, not_3_out;

  not not_1 (not_1_out, a);
  not not_2 (not_2_out, b);
  not not_3 (not_3_out, c);
  and and_1 (and_1_out, not_1_out, not_2_out);
  and and_2 (and_2_out, not_1_out, not_2_out);
  and and_3 (and_3_out, not_1_out, b);
  and and_4 (and_4_out, not_1_out, b);
  and and_5 (and_5_out, a, not_2_out);
  and and_6 (and_6_out, a, not_2_out);
  and and_7 (and_7_out, a, b);
  and and_8 (and_8_out, a, b);
  and and_9 (s0, and_1_out, not_3_out);
  and and_10 (s1, and_2_out, c);
  and and_11 (s2, and_3_out, not_3_out);
  and and_12 (s3, and_4_out, c);
  and and_13 (s4, and_5_out, not_3_out);
  and and_14 (s6, and_6_out, c);
  and and_15 (s7, and_7_out, not_3_out);
  and and_16 (s8, and_8_out, c);
endmodule
