// Digital circuit MUX 4 vers 1.dig as structural Verilog
module MUX_4_vers_1 (
  input  A,
  input  B,
  input  C,
  input  D,
  input  C1,
  input  C2,
  output S
);

  wire and_1_out, and_2_out, and_3_out, and_4_out, and_5_out, and_6_out, and_7_out, and_8_out, not_1_out,
       not_2_out, or_1_out, or_2_out;

  not not_1 (not_1_out, C1);
  not not_2 (not_2_out, C2);
  and and_1 (and_1_out, not_1_out, not_2_out);
  and and_2 (and_2_out, C1, not_2_out);
  and and_3 (and_3_out, not_1_out, C2);
  and and_4 (and_4_out, C2, C1);
  and and_5 (and_5_out, A, and_1_out);
  and and_6 (and_6_out, B, and_2_out);
  and and_7 (and_7_out, C, and_3_out);
  and and_8 (and_8_out, D, and_4_out);
  or or_1 (or_1_out, and_5_out, and_6_out);
  or or_2 (or_2_out, and_7_out, and_8_out);
  or or_3 (S, or_1_out, or_2_out);
endmodule
