// Digital circuit Mux 2 entrées.dig as structural Verilog
module \Mux_2_entrées  (
  input  a,
  input  b,
  input  s,
  output y
);

  wire and_1_out, and_2_out, not_1_out;

  not not_1 (not_1_out, s);
  and and_1 (and_1_out, a, s);
  and and_2 (and_2_out, b, not_1_out);
  or or_1 (y, and_1_out, and_2_out);
endmodule
