// Digital circuit UAL.dig as structural Verilog
module UAL (
  input  [7:0] A,
  input  [7:0] B,
  input  [7:0] S,
  input  C0,
  input  C1,
  output s0,
  output s1,
  output s2,
  output s3,
  output s4,
  output s5,
  output s6,
  output s7
);

  wire add_sub_1_p1, add_sub_1_p2, add_sub_1_p3, add_sub_1_p4, add_sub_1_p5, add_sub_1_p7, add_sub_1_p9,
       add_sub_1_p11, circuit_and_1_s0, circuit_and_1_s1, circuit_and_1_s2, circuit_and_1_s3,
       circuit_and_1_s4, circuit_and_1_s5, circuit_and_1_s6, circuit_and_1_s7, circuit_or_1_s0,
       circuit_or_1_s1, circuit_or_1_s2, circuit_or_1_s3, circuit_or_1_s4, circuit_or_1_s5, circuit_or_1_s6,
       circuit_or_1_s7, xor_8bits_1_s0, xor_8bits_1_s1, xor_8bits_1_s2, xor_8bits_1_s3, xor_8bits_1_s4,
       xor_8bits_1_s5, xor_8bits_1_s6, xor_8bits_1_s7;

  MUX_4_vers_1 mux_4_vers_1_1 (
    .A(add_sub_1_p1), .B(circuit_and_1_s7), .C(circuit_or_1_s7), .D(xor_8bits_1_s7), .C1(C0), .C2(C1), .S(s7));
  MUX_4_vers_1 mux_4_vers_1_2 (
    .A(add_sub_1_p2), .B(circuit_and_1_s6), .C(circuit_or_1_s6), .D(xor_8bits_1_s6), .C1(C0), .C2(C1), .S(s6));
  XOR_8bits xor_8bits_1 (
    .A(A), .B(B), .s0(xor_8bits_1_s0), .s1(xor_8bits_1_s1), .s2(xor_8bits_1_s2), .s3(xor_8bits_1_s3),
    .s4(xor_8bits_1_s4), .s5(xor_8bits_1_s5), .s6(xor_8bits_1_s6), .s7(xor_8bits_1_s7));
  MUX_4_vers_1 mux_4_vers_1_3 (
    .A(add_sub_1_p3), .B(circuit_and_1_s5), .C(circuit_or_1_s5), .D(xor_8bits_1_s5), .C1(C0), .C2(C1), .S(s5));
  Circuit_OR circuit_or_1 (
    .A(A), .B(B), .s0(circuit_or_1_s0), .s1(circuit_or_1_s1), .s2(circuit_or_1_s2), .s3(circuit_or_1_s3),
    .s4(circuit_or_1_s4), .s5(circuit_or_1_s5), .s6(circuit_or_1_s6), .s7(circuit_or_1_s7));
  MUX_4_vers_1 mux_4_vers_1_4 (
    .A(add_sub_1_p4), .B(circuit_and_1_s4), .C(circuit_or_1_s4), .D(xor_8bits_1_s4), .C1(C0), .C2(C1), .S(s4));
  Circuit_AND circuit_and_1 (
    .A(A), .B(B), .s0(circuit_and_1_s0), .s1(circuit_and_1_s1), .s2(circuit_and_1_s2), .s3(circuit_and_1_s3),
    .s4(circuit_and_1_s4), .s5(circuit_and_1_s5), .s6(circuit_and_1_s6), .s7(circuit_and_1_s7));
  MUX_4_vers_1 mux_4_vers_1_5 (
    .A(add_sub_1_p5), .B(circuit_and_1_s3), .C(circuit_or_1_s3), .D(xor_8bits_1_s3), .C1(C0), .C2(C1), .S(s3));
  // ADD_sub add_sub_1: pin names not known; wires that end beside it: add_sub_1_p1, add_sub_1_p2, add_sub_1_p3, add_sub_1_p4, add_sub_1_p5, A, add_sub_1_p7, B, add_sub_1_p9, S, add_sub_1_p11
  MUX_4_vers_1 mux_4_vers_1_6 (
    .B(circuit_and_1_s2), .C(circuit_or_1_s2), .D(xor_8bits_1_s2), .C1(C0), .C2(C1), .S(s2));  // open: A
  MUX_4_vers_1 mux_4_vers_1_7 (
    .A(add_sub_1_p9), .B(circuit_and_1_s1), .C(circuit_or_1_s1), .D(xor_8bits_1_s1), .C1(C0), .C2(C1), .S(s1));
  MUX_4_vers_1 mux_4_vers_1_8 (
    .A(add_sub_1_p11), .B(circuit_and_1_s0), .C(circuit_or_1_s0), .D(xor_8bits_1_s0), .C1(C0), .C2(C1), .S(s0));
endmodule
