// Digital circuit full adder .dig as structural Verilog
module full_adder (
  input  a,
  input  b,
  input  Cin,
  output s,
  output Cout
);

  wire and_1_out, and_2_out, xor_1_out;

  xor xor_1 (xor_1_out, a, b);
  and and_1 (and_1_out, xor_1_out, Cin);
  and and_2 (and_2_out, a, b);
  xor xor_2 (s, xor_1_out, Cin);
  or or_1 (Cout, and_1_out, and_2_out);
endmodule
