// Digital circuit Registre simple.dig as structural Verilog
module Registre_simple (
  input  e0,
  input  e1,
  input  e2,
  input  e3,
  input  e4,
  input  e5,
  input  e6,
  input  e7,
  input  CLK,
  output s0,
  output s1,
  output s2,
  output s3,
  output s4,
  output s5,
  output s6,
  output s7
);

  D_FF d_ff_1 (.D(e0), .C(CLK), .Q(s0));  // open: nQ
  D_FF d_ff_2 (.D(e1), .C(CLK), .Q(s1));  // open: nQ
  D_FF d_ff_3 (.D(e2), .C(CLK), .Q(s2));  // open: nQ
  D_FF d_ff_4 (.D(e3), .C(CLK), .Q(s3));  // open: nQ
  D_FF d_ff_5 (.D(e4), .C(CLK), .Q(s4));  // open: nQ
  D_FF d_ff_6 (.D(e5), .C(CLK), .Q(s5));  // open: nQ
  D_FF d_ff_7 (.D(e6), .C(CLK), .Q(s6));  // open: nQ
  D_FF d_ff_8 (.D(e7), .C(CLK), .Q(s7));  // open: nQ
endmodule
