// Digital circuit decalage à droite.dig as structural Verilog
module \decalage_à_droite  (
  input  e0,
  input  e1,
  input  e2,
  input  e3,
  input  e4,
  input  e5,
  input  e6,
  input  e7,
  input  Dec,
  input  W,
  input  left,
  output s0,
  output s1,
  output s2,
  output s3,
  output s4,
  output s5,
  output s6,
  output s7
);

  wire multiplexer_1_out, multiplexer_2_out, multiplexer_3_out, multiplexer_4_out, multiplexer_5_out,
       multiplexer_6_out, multiplexer_7_out, multiplexer_8_out, multiplexer_9_out, multiplexer_10_out,
       multiplexer_11_out, multiplexer_12_out, multiplexer_13_out, multiplexer_14_out, multiplexer_15_out,
       multiplexer_16_out, not_1_out, not_2_out;

  not not_1 (not_1_out, Dec);
  Multiplexer multiplexer_1 (.sel(not_1_out), .in_0(s1), .in_1(e0), .out(multiplexer_1_out));
  Multiplexer multiplexer_2 (.sel(not_1_out), .in_0(s2), .in_1(e1), .out(multiplexer_2_out));
  Multiplexer multiplexer_3 (.sel(not_1_out), .in_0(s3), .in_1(e2), .out(multiplexer_3_out));
  Multiplexer multiplexer_4 (.sel(not_1_out), .in_0(s4), .in_1(e3), .out(multiplexer_4_out));
  Multiplexer multiplexer_5 (.sel(not_1_out), .in_0(s5), .in_1(e4), .out(multiplexer_5_out));
  Multiplexer multiplexer_6 (.sel(not_1_out), .in_0(s6), .in_1(e5), .out(multiplexer_6_out));
  Multiplexer multiplexer_7 (.sel(not_1_out), .in_0(s7), .in_1(e6), .out(multiplexer_7_out));
  Multiplexer multiplexer_8 (.sel(not_1_out), .in_0(1'b0), .in_1(e7), .out(multiplexer_8_out));
  not not_2 (not_2_out, left);
  Multiplexer multiplexer_9 (.sel(not_2_out), .in_0(1'b0), .in_1(multiplexer_1_out), .out(multiplexer_9_out));
  Multiplexer multiplexer_10 (.sel(not_2_out), .in_0(s0), .in_1(multiplexer_2_out), .out(multiplexer_10_out));
  Multiplexer multiplexer_11 (.sel(not_2_out), .in_0(s1), .in_1(multiplexer_3_out), .out(multiplexer_11_out));
  Multiplexer multiplexer_12 (.sel(not_2_out), .in_0(s2), .in_1(multiplexer_4_out), .out(multiplexer_12_out));
  Multiplexer multiplexer_13 (.sel(not_2_out), .in_0(s3), .in_1(multiplexer_5_out), .out(multiplexer_13_out));
  Multiplexer multiplexer_14 (.sel(not_2_out), .in_0(s4), .in_1(multiplexer_6_out), .out(multiplexer_14_out));
  Multiplexer multiplexer_15 (.sel(not_2_out), .in_0(s5), .in_1(multiplexer_7_out), .out(multiplexer_15_out));
  Multiplexer multiplexer_16 (.sel(not_2_out), .in_0(s6), .in_1(multiplexer_8_out), .out(multiplexer_16_out));
  D_FF d_ff_1 (.D(multiplexer_9_out), .C(W), .Q(s0));  // open: nQ
  D_FF d_ff_2 (.D(multiplexer_10_out), .C(W), .Q(s1));  // open: nQ
  D_FF d_ff_3 (.D(multiplexer_11_out), .C(W), .Q(s2));  // open: nQ
  D_FF d_ff_4 (.D(multiplexer_12_out), .C(W), .Q(s3));  // open: nQ
  D_FF d_ff_5 (.D(multiplexer_13_out), .C(W), .Q(s4));  // open: nQ
  D_FF d_ff_6 (.D(multiplexer_14_out), .C(W), .Q(s5));  // open: nQ
  D_FF d_ff_7 (.D(multiplexer_15_out), .C(W), .Q(s6));  // open: nQ
  D_FF d_ff_8 (.D(multiplexer_16_out), .C(W), .Q(s7));  // open: nQ
endmodule
