// Digital circuit Circuit_complet_2024.dig as structural Verilog
module Circuit_complet_2024 (
  input  W_BLOC,
  input  in_3,
  output [31:0] x5,
  output [31:0] x7,
  output [31:0] x6
);

  wire c_mux_im_1_p5, c_mux_im_1_p6, cb_callback_1_p3, cb_callback_1_p4, cb_callback_1_p5, cb_callback_1_p6,
       cb_callback_1_p7, cb_ex_1_p2, cb_ex_1_p3, cb_mem_1_p1, cb_mem_1_p2, cb_mem_1_p3, cb_mem_1_p4,
       cb_mem_1_p8, cb_mem_1_p9, delay_1_out, id_reg_1_p10, id_reg_1_p11, if_reg_1_p5, mem_reg_1_p2,
       mem_reg_1_p9, mem_reg_1_p11, multiplexer_7_out, not_1_out, not_2_out, ual_1_p5, ual_1_p10;
  wire [1:0] c_mux_im_1_p1, cb_ex_1_p4;
  wire [2:0] id_reg_1_p9, multiplexer_5_out;
  wire [4:0] mem_reg_1_p10;
  wire [6:0] id_reg_1_p8;
  wire [7:0] PC_q_2;
  wire [31:0] add_1_s, add_2_s, banc_de_registres_1_src1, banc_de_registres_1_src2, bitextender_1_out,
       bitextender_2_out, bitextender_3_out, bitextender_4_out, cb_mem_1_p5, cb_mem_1_p6, delay_2_out,
       id_reg_1_p12, id_reg_1_p13, if_reg_1_p4, mem_reg_1_p8, mem_reg_1_p12, mem_reg_1_p13,
       multiplexer_1_out, multiplexer_2_out, multiplexer_3_out, multiplexer_4_out, multiplexer_6_out,
       multiplexer_8_out, multiplexer_9_out, multiplexer_10_out, PC_q, ramsingleportsel_1_d,
       ramsingleportsel_2_d, sub_1_s;

  Sub #(.Bits(32)) sub_1 (.a(multiplexer_10_out), .b(32'h10), .c_i(1'b0), .s(sub_1_s));  // open: c_o
  Multiplexer #(.Bits(32)) multiplexer_1 (
    .sel(cb_callback_1_p5), .in_0(32'h4), .in_1(sub_1_s), .out(multiplexer_1_out));
  Add #(.Bits(32)) add_1 (
    .a(multiplexer_1_out), .b({PC_q[31:10], PC_q_2, PC_q[1:0]}), .c_i(1'b0), .s(add_1_s));  // open: c_o
  Multiplexer #(.Bits(32)) multiplexer_2 (
    .sel(cb_callback_1_p6), .in_0(add_1_s), .in_1(multiplexer_10_out), .out(multiplexer_2_out));
  Delay delay_1 (.in(W_BLOC), .out(delay_1_out));
  Multiplexer #(.Bits(32)) multiplexer_3 (
    .sel(in_3), .in_0(multiplexer_2_out), .in_1({32{1'b0}}), .out(multiplexer_3_out));
  D_FF #(.Bits(32)) PC (.D(multiplexer_3_out), .C(delay_1_out), .Q({PC_q[31:10], PC_q_2, PC_q[1:0]}));  // open: nQ
  RAMSinglePortSel #(.AddrBits(8), .Bits(32)) ramsingleportsel_1 (
    .A(PC_q_2), .CS(1'b1), .WE(not_1_out), .OE(1'b1), .D(ramsingleportsel_1_d));
  not not_1 (not_1_out, 1'b1);
  Add #(.Bits(32)) add_2 (.a({PC_q[31:10], PC_q_2, PC_q[1:0]}), .b(32'h4), .c_i(1'b0), .s(add_2_s));  // open: c_o
  // IF_REG if_reg_1: pin names not known; wires that end beside it: ramsingleportsel_1_d, add_2_s, W_BLOC, if_reg_1_p4, if_reg_1_p5
  Banc_De_Registres banc_de_registres_1 (
    .Wreg(cb_callback_1_p7), .rd(mem_reg_1_p10), .rs1(if_reg_1_p4[19:15]), .rs2(if_reg_1_p4[24:20]),
    .res(multiplexer_9_out), .src1(banc_de_registres_1_src1), .src2(banc_de_registres_1_src2), .x5(x5),
    .x6(x6), .x7(x7));
  BitExtender #(.inputBits(12), .outputBits(32)) bitextender_1 (.in(if_reg_1_p4[31:20]), .out(bitextender_1_out));
  BitExtender #(.inputBits(12), .outputBits(32)) bitextender_2 (
    .in({if_reg_1_p4[31:25], if_reg_1_p4[11:7]}), .out(bitextender_2_out));
  BitExtender #(.inputBits(14), .outputBits(32)) bitextender_3 (
    .in({if_reg_1_p4[31], if_reg_1_p4[7], if_reg_1_p4[30:25], if_reg_1_p4[11:8], 2'b00}),
    .out(bitextender_3_out));
  BitExtender #(.inputBits(22), .outputBits(32)) bitextender_4 (
    .in({if_reg_1_p4[31], if_reg_1_p4[19:12], if_reg_1_p4[20], if_reg_1_p4[30:21], 2'b00}),
    .out(bitextender_4_out));
  Multiplexer #(.Selector_Bits(2), .Bits(32)) multiplexer_4 (
    .sel(c_mux_im_1_p1), .in_0(bitextender_1_out), .in_1(bitextender_2_out), .in_2(bitextender_3_out),
    .in_3(bitextender_4_out), .out(multiplexer_4_out));
  // C_MUX_IM c_mux_im_1: pin names not known; wires that end beside it: c_mux_im_1_p1, if_reg_1_p4[6:0], if_reg_1_p4[14:12], if_reg_1_p4[31:25], c_mux_im_1_p5, c_mux_im_1_p6
  // ID_REG id_reg_1: pin names not known; wires that end beside it: banc_de_registres_1_src1, if_reg_1_p5, W_BLOC, banc_de_registres_1_src2, multiplexer_4_out, if_reg_1_p4[11:7], if_reg_1_p4[6:0], id_reg_1_p8, id_reg_1_p9, id_reg_1_p10, id_reg_1_p11, id_reg_1_p12, id_reg_1_p13
  // CB_EX cb_ex_1: pin names not known; wires that end beside it: id_reg_1_p10, cb_ex_1_p2, cb_ex_1_p3, cb_ex_1_p4
  Multiplexer #(.Bits(3)) multiplexer_5 (.sel(cb_ex_1_p3), .in_0(id_reg_1_p9), .in_1(3'b000), .out(multiplexer_5_out));
  Multiplexer #(.Bits(32)) multiplexer_6 (
    .sel(cb_ex_1_p2), .in_0(id_reg_1_p13), .in_1(id_reg_1_p12), .out(multiplexer_6_out));
  Multiplexer #(.Selector_Bits(2)) multiplexer_7 (
    .sel(cb_ex_1_p4), .in_0(1'b0), .in_1(id_reg_1_p8[5]), .in_2(1'b1), .in_3(1'b0), .out(multiplexer_7_out));
  // UAL ual_1: pin names not known; wires that end beside it: multiplexer_7_out, multiplexer_5_out, c_mux_im_1_p5, multiplexer_6_out, ual_1_p5, ual_1_p5, c_mux_im_1_p6, W_BLOC, id_reg_1_p13, ual_1_p10, id_reg_1_p11, id_reg_1_p10
  // BRANCH branch_1: pin names not known; wires that end beside it: id_reg_1_p9, ual_1_p5, ual_1_p10, id_reg_1_p12
  EX_REG ex_reg_1 ();
  // CB_MEM cb_mem_1: pin names not known; wires that end beside it: cb_mem_1_p1, cb_mem_1_p2, cb_mem_1_p3, cb_mem_1_p4, cb_mem_1_p5, cb_mem_1_p6, cb_mem_1_p2, cb_mem_1_p8, cb_mem_1_p9
  Delay #(.Bits(32), .delayTime(2)) delay_2 (.in(cb_mem_1_p6), .out(delay_2_out));
  RAMSinglePortSel #(.AddrBits(8), .Bits(32)) ramsingleportsel_2 (
    .A(delay_2_out[9:2]), .CS(1'b1), .WE(cb_mem_1_p9), .OE(not_2_out), .D(ramsingleportsel_2_d));
  not not_2 (not_2_out, cb_mem_1_p9);
  assign ramsingleportsel_2_d = cb_mem_1_p9 ? cb_mem_1_p5 : 32'bz;  // Driver driver_1
  Multiplexer #(.Bits(32)) multiplexer_8 (
    .sel(cb_mem_1_p8), .in_0(cb_mem_1_p6), .in_1(ramsingleportsel_2_d), .out(multiplexer_8_out));
  // MEM_REG mem_reg_1: pin names not known; wires that end beside it: multiplexer_8_out, mem_reg_1_p2, W_BLOC, cb_mem_1_p4, cb_mem_1_p3, cb_mem_1_p2, cb_mem_1_p1, mem_reg_1_p8, mem_reg_1_p9, mem_reg_1_p10, mem_reg_1_p11, mem_reg_1_p12, mem_reg_1_p13
  Multiplexer #(.Bits(32)) multiplexer_9 (
    .sel(cb_callback_1_p4), .in_0(mem_reg_1_p12), .in_1(mem_reg_1_p13), .out(multiplexer_9_out));
  // CB_CALLBACK cb_callback_1: pin names not known; wires that end beside it: mem_reg_1_p9, mem_reg_1_p11, cb_callback_1_p3, cb_callback_1_p4, cb_callback_1_p5, cb_callback_1_p6, cb_callback_1_p7
  Multiplexer #(.Bits(32)) multiplexer_10 (
    .sel(cb_callback_1_p3), .in_0(mem_reg_1_p8), .in_1(mem_reg_1_p12), .out(multiplexer_10_out));

  // Notes on the sheet:
  //   TYPE I
  //   TYPE S
  //   TYPE B
  //   TYPE J
endmodule
