// Digital circuit Add 1bit.dig as structural Verilog
module Add_1bit (
  input  a,
  input  b,
  input  Cin,
  output s,
  output Cout,
  output P,
  output G
);

  wire and_2_out;

  xor xor_1 (P, a, b);
  and and_1 (G, P, Cin);
  and and_2 (and_2_out, a, b);
  xor xor_2 (s, P, Cin);
  or or_1 (Cout, G, and_2_out);
endmodule
