// Digital circuit Add(PG) 1 bit.dig as structural Verilog
module Add_PG__1_bit (
  input  a,
  input  b,
  input  Cin,
  output s,
  output G,
  output P
);

  xor xor_1 (P, a, b);
  and and_1 (G, a, b);
  xor xor_2 (s, P, Cin);
endmodule
