// Digital circuit Add(PG) 8 bit.dig as structural Verilog
module Add_PG__8_bit (
  input  a0,
  input  b0,
  input  C0,
  input  a1,
  input  b1,
  input  a2,
  input  b2,
  input  a3,
  input  b3,
  input  a4,
  input  b4,
  input  a5,
  input  b5,
  input  a6,
  input  b6,
  input  a7,
  input  b7,
  output R,
  output s0,
  output s1,
  output s2,
  output s3,
  output s4,
  output s5,
  output s6,
  output s7
);

  wire add_pg__1_bit_1_g, add_pg__1_bit_1_p, add_pg__1_bit_2_g, add_pg__1_bit_2_p, add_pg__1_bit_3_g,
       add_pg__1_bit_3_p, add_pg__1_bit_4_g, add_pg__1_bit_4_p, add_pg__1_bit_5_g, add_pg__1_bit_5_p,
       add_pg__1_bit_6_g, add_pg__1_bit_6_p, add_pg__1_bit_7_g, add_pg__1_bit_7_p, add_pg__1_bit_8_g,
       add_pg__1_bit_8_p;

  Add_PG__1_bit add_pg__1_bit_1 (.a(a0), .b(b0), .Cin(C0), .s(s0), .G(add_pg__1_bit_1_g), .P(add_pg__1_bit_1_p));
  Add_PG__1_bit add_pg__1_bit_2 (.a(a1), .b(b1), .Cin(C0), .s(s1), .G(add_pg__1_bit_2_g), .P(add_pg__1_bit_2_p));
  Add_PG__1_bit add_pg__1_bit_3 (.a(a2), .b(b2), .Cin(C0), .s(s2), .G(add_pg__1_bit_3_g), .P(add_pg__1_bit_3_p));
  Add_PG__1_bit add_pg__1_bit_4 (.a(a3), .b(b3), .Cin(C0), .s(s3), .G(add_pg__1_bit_4_g), .P(add_pg__1_bit_4_p));
  Add_PG__1_bit add_pg__1_bit_5 (.a(a4), .b(b4), .Cin(C0), .s(s4), .G(add_pg__1_bit_5_g), .P(add_pg__1_bit_5_p));
  Add_PG__1_bit add_pg__1_bit_6 (.a(a5), .b(b5), .Cin(C0), .s(s5), .G(add_pg__1_bit_6_g), .P(add_pg__1_bit_6_p));
  Add_PG__1_bit add_pg__1_bit_7 (.a(a6), .b(b6), .Cin(C0), .s(s6), .G(add_pg__1_bit_7_g), .P(add_pg__1_bit_7_p));
  cc8bits cc8bits_1 (
    .G0(add_pg__1_bit_1_g), .P0(add_pg__1_bit_1_p), .G1(add_pg__1_bit_2_g), .P1(add_pg__1_bit_2_p),
    .G2(add_pg__1_bit_3_g), .P2(add_pg__1_bit_3_p), .G3(add_pg__1_bit_4_g), .P3(add_pg__1_bit_4_p), .C0(C0),
    .G4(add_pg__1_bit_5_g), .P4(add_pg__1_bit_5_p), .G5(add_pg__1_bit_6_g), .P5(add_pg__1_bit_6_p),
    .G6(add_pg__1_bit_7_g), .P6(add_pg__1_bit_7_p), .G7(add_pg__1_bit_8_g), .P7(add_pg__1_bit_8_p), .C8(R));
  Add_PG__1_bit add_pg__1_bit_8 (.a(a7), .b(b7), .Cin(C0), .s(s7), .G(add_pg__1_bit_8_g), .P(add_pg__1_bit_8_p));
endmodule
