// Digital circuit Barrel shifter.dig as structural Verilog
module Barrel_shifter (
  input  e0,
  input  [1:0] dec,
  input  e1,
  input  e2,
  input  e3,
  input  e4,
  input  e5,
  input  e6,
  input  e7,
  output s0,
  output s1,
  output s2,
  output s3,
  output s4,
  output s5,
  output s6,
  output s7
);

  wire multiplexer_1_out, multiplexer_3_out, multiplexer_5_out, multiplexer_7_out, multiplexer_9_out,
       multiplexer_11_out, multiplexer_13_out, multiplexer_15_out;

  Multiplexer multiplexer_1 (.sel(dec[0]), .in_0(e7), .in_1(e6), .out(multiplexer_1_out));
  Multiplexer multiplexer_2 (.sel(dec[1]), .in_0(multiplexer_1_out), .in_1(multiplexer_5_out), .out(s7));
  Multiplexer multiplexer_3 (.sel(dec[0]), .in_0(e6), .in_1(e5), .out(multiplexer_3_out));
  Multiplexer multiplexer_4 (.sel(dec[1]), .in_0(multiplexer_3_out), .in_1(multiplexer_7_out), .out(s6));
  Multiplexer multiplexer_5 (.sel(dec[0]), .in_0(e5), .in_1(e4), .out(multiplexer_5_out));
  Multiplexer multiplexer_6 (.sel(dec[1]), .in_0(multiplexer_5_out), .in_1(multiplexer_9_out), .out(s5));
  Multiplexer multiplexer_7 (.sel(dec[0]), .in_0(e4), .in_1(e3), .out(multiplexer_7_out));
  Multiplexer multiplexer_8 (.sel(dec[1]), .in_0(multiplexer_7_out), .in_1(multiplexer_11_out), .out(s4));
  Multiplexer multiplexer_9 (.sel(dec[0]), .in_0(e3), .in_1(e2), .out(multiplexer_9_out));
  Multiplexer multiplexer_10 (.sel(dec[1]), .in_0(multiplexer_9_out), .in_1(multiplexer_13_out), .out(s3));
  Multiplexer multiplexer_11 (.sel(dec[0]), .in_0(e2), .in_1(e1), .out(multiplexer_11_out));
  Multiplexer multiplexer_12 (.sel(dec[1]), .in_0(multiplexer_11_out), .in_1(multiplexer_15_out), .out(s2));
  Multiplexer multiplexer_13 (.sel(dec[0]), .in_0(e1), .in_1(e0), .out(multiplexer_13_out));
  Multiplexer multiplexer_14 (.sel(dec[1]), .in_0(multiplexer_13_out), .in_1(1'b0), .out(s1));
  Multiplexer multiplexer_15 (.sel(dec[0]), .in_0(e0), .in_1(1'b0), .out(multiplexer_15_out));
  Multiplexer multiplexer_16 (.sel(dec[1]), .in_0(multiplexer_15_out), .in_1(1'b0), .out(s0));
endmodule
