// Digital circuit Division 2.dig as structural Verilog
module Division_2 (
  input  a0,
  input  a1,
  input  a2,
  input  a3,
  input  [1:0] c,
  output s0,
  output s1,
  output s2,
  output s3
);

  wire multiplexer_1_out, multiplexer_4_out, multiplexer_5_out, multiplexer_7_out;

  Multiplexer multiplexer_1 (.sel(c[0]), .in_0(a3), .in_1(1'b0), .out(multiplexer_1_out));
  Multiplexer multiplexer_2 (.sel(c[1]), .in_0(multiplexer_1_out), .in_1(1'b0), .out(s3));
  Multiplexer multiplexer_3 (.sel(c[1]), .in_0(multiplexer_4_out), .in_1(1'b0), .out(s2));
  Multiplexer multiplexer_4 (.sel(c[0]), .in_0(a2), .in_1(a3), .out(multiplexer_4_out));
  Multiplexer multiplexer_5 (.sel(c[0]), .in_0(a1), .in_1(a2), .out(multiplexer_5_out));
  Multiplexer multiplexer_6 (.sel(c[1]), .in_0(multiplexer_5_out), .in_1(multiplexer_1_out), .out(s1));
  Multiplexer multiplexer_7 (.sel(c[0]), .in_0(a0), .in_1(a1), .out(multiplexer_7_out));
  Multiplexer multiplexer_8 (.sel(c[1]), .in_0(multiplexer_7_out), .in_1(multiplexer_4_out), .out(s0));
endmodule
