// Digital circuit Division.dig as structural Verilog
module Division (
  input  a0,
  input  a1,
  input  a2,
  input  a3,
  input  c,
  output s0,
  output s1,
  output s2,
  output s3
);

  Multiplexer multiplexer_1 (.sel(c), .in_0(a3), .in_1(1'b0), .out(s3));
  Multiplexer multiplexer_2 (.sel(c), .in_0(a2), .in_1(a3), .out(s2));
  Multiplexer multiplexer_3 (.sel(c), .in_0(a1), .in_1(a2), .out(s1));
  Multiplexer multiplexer_4 (.sel(c), .in_0(a0), .in_1(a1), .out(s0));
endmodule
