// Digital circuit afficheur 1.dig as structural Verilog
module afficheur_1 (
  input  Res,
  input  CLK,
  output g,
  output f,
  output e,
  output d,
  output c,
  output b,
  output a,
  output s2,
  output s1,
  output s0
);

  wire and_1_out, and_2_out, and_3_out, and_4_out, and_5_out, and_6_out, and_7_out, and_8_out, and_9_out,
       and_10_out, and_11_out, and_12_out, and_13_out, and_14_out, and_15_out, and_16_out, and_17_out,
       and_18_out, and_19_out, and_20_out, and_21_out, and_22_out, D0_nq, D1_nq, D2_nq, not_1_out, or_1_out,
       or_2_out, xor_1_out;

  not not_1 (not_1_out, Res);
  and and_1 (and_1_out, s2, D0_nq);
  and and_2 (and_2_out, s2, D1_nq);
  and and_3 (and_3_out, s0, s1);
  and and_4 (and_4_out, D2_nq, not_1_out);
  and and_5 (and_5_out, and_1_out, not_1_out);
  and and_6 (and_6_out, and_2_out, not_1_out);
  and and_7 (and_7_out, and_3_out, and_4_out);
  or or_1 (or_1_out, and_5_out, and_6_out);
  xor xor_1 (xor_1_out, s1, s0);
  or or_2 (or_2_out, or_1_out, and_7_out);
  and and_8 (and_8_out, xor_1_out, not_1_out);
  and and_9 (and_9_out, not_1_out, D0_nq);
  D_FF D2 (.D(or_2_out), .C(CLK), .Q(s2), .nQ(D2_nq));
  D_FF D1 (.D(and_8_out), .C(CLK), .Q(s1), .nQ(D1_nq));
  D_FF D0 (.D(and_9_out), .C(CLK), .Q(s0), .nQ(D0_nq));
  and and_10 (and_10_out, not_1_out, D2_nq);
  and and_11 (and_11_out, D1_nq, D0_nq);
  and and_12 (and_12_out, not_1_out, D2_nq);
  and and_13 (and_13_out, D1_nq, s0);
  and and_14 (and_14_out, not_1_out, s2);
  and and_15 (and_15_out, D1_nq, s0);
  and and_16 (and_16_out, not_1_out, s2);
  and and_17 (and_17_out, D1_nq, D0_nq);
  and and_18 (and_18_out, not_1_out, D2_nq);
  and and_19 (and_19_out, s1, s0);
  and and_20 (and_20_out, not_1_out, s2);
  and and_21 (and_21_out, s1, s0);
  and and_22 (and_22_out, not_1_out, s1);
  and and_23 (a, and_10_out, and_11_out);
  and and_24 (b, and_12_out, and_13_out);
  and and_25 (c, and_14_out, and_15_out);
  and and_26 (d, and_16_out, and_17_out);
  and and_27 (e, and_18_out, and_19_out);
  and and_28 (f, and_20_out, and_21_out);
  and and_29 (g, and_22_out, D0_nq);
  Seven_Seg seven_seg_1 (.a(a), .b(b), .c(c), .d(d), .e(e), .f(f), .g(g), .dp(1'b0));
endmodule
