// Digital circuit afficheur inv.dig as structural Verilog
module afficheur_inv (
  input  Res,
  input  CLK,
  input  Inv,
  output s2,
  output s1,
  output s0,
  output f,
  output c,
  output d,
  output e,
  output g,
  output b,
  output a
);

  wire and_1_out, and_2_out, and_3_out, and_4_out, and_5_out, and_6_out, and_7_out, and_8_out, and_9_out,
       and_10_out, and_11_out, and_12_out, and_13_out, and_14_out, and_15_out, and_16_out, and_17_out,
       and_18_out, and_19_out, and_20_out, and_21_out, and_22_out, and_23_out, and_24_out, and_25_out,
       and_26_out, and_27_out, and_28_out, and_29_out, and_30_out, and_31_out, and_32_out, and_33_out,
       and_34_out, D0_nq, D1_nq, D2_nq, not_1_out, not_2_out, or_1_out, or_2_out, or_3_out, or_4_out,
       or_5_out, or_6_out, xor_1_out;

  not not_1 (not_1_out, Res);
  not not_2 (not_2_out, Inv);
  and and_1 (and_1_out, s2, D0_nq);
  and and_2 (and_2_out, s2, D1_nq);
  and and_3 (and_3_out, s0, s1);
  and and_4 (and_4_out, D2_nq, not_1_out);
  and and_5 (and_5_out, and_1_out, not_1_out);
  and and_6 (and_6_out, and_2_out, not_1_out);
  and and_7 (and_7_out, and_3_out, and_4_out);
  or or_1 (or_1_out, and_5_out, and_6_out);
  xor xor_1 (xor_1_out, s1, s0);
  or or_2 (or_2_out, or_1_out, and_7_out);
  and and_8 (and_8_out, not_1_out, D0_nq);
  and and_9 (and_9_out, xor_1_out, not_1_out);
  D_FF D2 (.D(or_2_out), .C(CLK), .Q(s2), .nQ(D2_nq));
  D_FF D1 (.D(and_9_out), .C(CLK), .Q(s1), .nQ(D1_nq));
  D_FF D0 (.D(and_8_out), .C(CLK), .Q(s0), .nQ(D0_nq));
  and and_10 (and_10_out, not_2_out, D2_nq);
  and and_11 (and_11_out, Inv, s2);
  and and_12 (and_12_out, not_2_out, D2_nq);
  and and_13 (and_13_out, Inv, s2);
  and and_14 (and_14_out, Inv, D2_nq);
  and and_15 (and_15_out, not_2_out, s2);
  and and_16 (and_16_out, Inv, D2_nq);
  and and_17 (and_17_out, not_2_out, s2);
  and and_18 (and_18_out, and_10_out, D1_nq);
  and and_19 (and_19_out, and_11_out, s1);
  and and_20 (and_20_out, and_12_out, s1);
  and and_21 (and_21_out, and_13_out, D1_nq);
  and and_22 (and_22_out, and_14_out, D1_nq);
  and and_23 (and_23_out, and_15_out, D1_nq);
  and and_24 (and_24_out, and_16_out, D1_nq);
  and and_25 (and_25_out, and_17_out, s0);
  and and_26 (and_26_out, not_1_out, D2_nq);
  and and_27 (and_27_out, D1_nq, D0_nq);
  and and_28 (and_28_out, not_1_out, D0_nq);
  or or_3 (or_3_out, and_18_out, and_19_out);
  and and_29 (and_29_out, not_1_out, s1);
  and and_30 (and_30_out, not_1_out, s0);
  or or_4 (or_4_out, and_20_out, and_21_out);
  and and_31 (and_31_out, not_1_out, s2);
  and and_32 (and_32_out, D1_nq, D1_nq);
  and and_33 (and_33_out, not_1_out, s0);
  or or_5 (or_5_out, and_22_out, and_23_out);
  and and_34 (and_34_out, Inv, s0);
  or or_6 (or_6_out, and_24_out, and_25_out);
  and and_35 (a, and_26_out, and_27_out);
  and and_36 (b, and_28_out, or_3_out);
  and and_37 (g, and_29_out, D0_nq);
  and and_38 (e, and_30_out, or_4_out);
  and and_39 (d, and_31_out, and_32_out);
  and and_40 (c, and_33_out, or_5_out);
  and and_41 (f, and_34_out, or_6_out);
  Seven_Seg seven_seg_1 (.a(a), .b(b), .c(g), .d(e), .e(d), .f(c), .g(f), .dp(1'b0));
endmodule
