// Digital circuit comparateur 8bits.dig as structural Verilog
module comparateur_8bits (
  input  a0,
  input  b0,
  input  a1,
  input  b1,
  input  a2,
  input  b2,
  input  a3,
  input  b3,
  output eq,
  output gt,
  output lt
);

  wire and_1_out, and_2_out, and_3_out, and_4_out, and_5_out, and_6_out, and_7_out, and_8_out, and_9_out,
       and_10_out, and_11_out, and_12_out, and_13_out, and_14_out, comparateur_1bit_1_eq,
       comparateur_1bit_1_gt, comparateur_1bit_1_lt, comparateur_1bit_2_eq, comparateur_1bit_2_gt,
       comparateur_1bit_2_lt, comparateur_1bit_3_eq, comparateur_1bit_3_gt, comparateur_1bit_3_lt,
       comparateur_1bit_4_eq, comparateur_1bit_4_gt, comparateur_1bit_4_lt, or_1_out, or_2_out, or_3_out,
       or_4_out;

  comparateur_1bit comparateur_1bit_1 (
    .a(a0), .b(b0), .gt(comparateur_1bit_1_gt), .eq(comparateur_1bit_1_eq), .lt(comparateur_1bit_1_lt));
  comparateur_1bit comparateur_1bit_2 (
    .a(a1), .b(b1), .gt(comparateur_1bit_2_gt), .eq(comparateur_1bit_2_eq), .lt(comparateur_1bit_2_lt));
  comparateur_1bit comparateur_1bit_3 (
    .a(a2), .b(b2), .gt(comparateur_1bit_3_gt), .eq(comparateur_1bit_3_eq), .lt(comparateur_1bit_3_lt));
  comparateur_1bit comparateur_1bit_4 (
    .a(a3), .b(b3), .gt(comparateur_1bit_4_gt), .eq(comparateur_1bit_4_eq), .lt(comparateur_1bit_4_lt));
  and and_1 (and_1_out, comparateur_1bit_1_eq, comparateur_1bit_2_gt);
  and and_2 (and_2_out, comparateur_1bit_1_eq, comparateur_1bit_2_eq);
  and and_3 (and_3_out, comparateur_1bit_1_eq, comparateur_1bit_2_eq);
  and and_4 (and_4_out, comparateur_1bit_3_eq, comparateur_1bit_4_gt);
  and and_5 (and_5_out, comparateur_1bit_1_eq, comparateur_1bit_2_eq);
  and and_6 (and_6_out, comparateur_1bit_3_eq, comparateur_1bit_4_eq);
  and and_7 (and_7_out, comparateur_1bit_1_eq, comparateur_1bit_2_lt);
  and and_8 (and_8_out, comparateur_1bit_1_eq, comparateur_1bit_2_eq);
  and and_9 (and_9_out, comparateur_1bit_1_eq, comparateur_1bit_2_eq);
  and and_10 (and_10_out, comparateur_1bit_3_eq, comparateur_1bit_4_lt);
  and and_11 (and_11_out, and_2_out, comparateur_1bit_3_gt);
  and and_12 (and_12_out, and_3_out, and_4_out);
  and and_13 (and_13_out, and_8_out, comparateur_1bit_3_lt);
  and and_14 (and_14_out, and_9_out, and_10_out);
  and and_15 (eq, and_5_out, and_6_out);
  or or_1 (or_1_out, comparateur_1bit_1_gt, and_1_out);
  or or_2 (or_2_out, and_11_out, and_12_out);
  or or_3 (or_3_out, comparateur_1bit_1_lt, and_7_out);
  or or_4 (or_4_out, and_13_out, and_14_out);
  or or_5 (gt, or_1_out, or_2_out);
  or or_6 (lt, or_3_out, or_4_out);
endmodule
