// Digital circuit Mux 8 vers 3.dig as structural Verilog
module Mux_8_vers_3 (
  input  e0,
  input  e1,
  input  s0,
  input  s1,
  input  s2,
  input  e2,
  input  e3,
  input  e4,
  input  e5,
  input  e6,
  input  e7,
  output y
);

  wire multiplexer_1_out, multiplexer_2_out, multiplexer_3_out, multiplexer_4_out, multiplexer_5_out,
       multiplexer_6_out;

  Multiplexer multiplexer_1 (.sel(s0), .in_0(e0), .in_1(e1), .out(multiplexer_1_out));
  Multiplexer multiplexer_2 (.sel(s0), .in_0(e2), .in_1(e3), .out(multiplexer_2_out));
  Multiplexer multiplexer_3 (.sel(s0), .in_0(e4), .in_1(e5), .out(multiplexer_3_out));
  Multiplexer multiplexer_4 (.sel(s0), .in_0(e6), .in_1(e7), .out(multiplexer_4_out));
  Multiplexer multiplexer_5 (.sel(s1), .in_0(multiplexer_1_out), .in_1(multiplexer_2_out), .out(multiplexer_5_out));
  Multiplexer multiplexer_6 (.sel(s1), .in_0(multiplexer_3_out), .in_1(multiplexer_4_out), .out(multiplexer_6_out));
  Multiplexer multiplexer_7 (.sel(s2), .in_0(multiplexer_5_out), .in_1(multiplexer_6_out), .out(y));
endmodule
