// Digital circuit Registre 8bits.dig as structural Verilog
module Registre_8bits (
  input  D0,
  input  D1,
  input  D2,
  input  D3,
  input  D4,
  input  D5,
  input  D6,
  input  D7,
  input  CLK,
  output s0,
  output s1,
  output s2,
  output s3,
  output s4,
  output s5,
  output s6,
  output s7
);

  D_FF d_ff_1 (.D(D0), .C(CLK), .Q(s0));  // open: nQ
  D_FF d_ff_2 (.D(D1), .C(CLK), .Q(s1));  // open: nQ
  D_FF d_ff_3 (.D(D2), .C(CLK), .Q(s2));  // open: nQ
  D_FF d_ff_4 (.D(D3), .C(CLK), .Q(s3));  // open: nQ
  D_FF d_ff_5 (.D(D4), .C(CLK), .Q(s4));  // open: nQ
  D_FF d_ff_6 (.D(D5), .C(CLK), .Q(s5));  // open: nQ
  D_FF d_ff_7 (.D(D6), .C(CLK), .Q(s6));  // open: nQ
  D_FF d_ff_8 (.D(D7), .C(CLK), .Q(s7));  // open: nQ
endmodule
