// Digital circuit add 8bits.dig as structural Verilog
module add_8bits (
  input  a0,
  input  b0,
  input  sub,
  input  a1,
  input  b1,
  input  a2,
  input  b2,
  input  a3,
  input  b3,
  input  a4,
  input  b4,
  input  a5,
  input  b5,
  input  a6,
  input  b6,
  input  a7,
  input  b7,
  output Cout
);

  wire add_1bit_2_cout, add_1bit_3_cout, add_1bit_4_cout, add_1bit_5_cout, add_1bit_6_cout, add_1bit_7_cout,
       add_1bit_8_cout;

  Add_1bit add_1bit_1 (.a(a7), .b(b7), .Cin(add_1bit_2_cout), .s(Cout));  // open: Cout, P, G
  Add_1bit add_1bit_2 (.a(a6), .b(b6), .Cin(add_1bit_3_cout), .Cout(add_1bit_2_cout));  // open: s, P, G
  Add_1bit add_1bit_3 (.a(a5), .b(b5), .Cin(add_1bit_4_cout), .Cout(add_1bit_3_cout));  // open: s, P, G
  Add_1bit add_1bit_4 (.a(a4), .b(b4), .Cin(add_1bit_5_cout), .Cout(add_1bit_4_cout));  // open: s, P, G
  Add_1bit add_1bit_5 (.a(a3), .b(b3), .Cin(add_1bit_6_cout), .Cout(add_1bit_5_cout));  // open: s, P, G
  Add_1bit add_1bit_6 (.a(a2), .b(b2), .Cin(add_1bit_7_cout), .Cout(add_1bit_6_cout));  // open: s, P, G
  Add_1bit add_1bit_7 (.a(a1), .b(b1), .Cin(add_1bit_8_cout), .Cout(add_1bit_7_cout));  // open: s, P, G
  Add_1bit add_1bit_8 (.a(a0), .b(b0), .Cin(sub), .Cout(add_1bit_8_cout));  // open: s, P, G
endmodule
