// Digital circuit cc 1bit.dig as structural Verilog
module cc_1bit (
  input  P,
  input  G,
  input  Cin,
  output Cout
);

  wire and_1_out;

  and and_1 (and_1_out, P, Cin);
  or or_1 (Cout, G, and_1_out);
endmodule
