// Digital circuit cc8bits.dig as structural Verilog
module cc8bits (
  input  G0,
  input  P0,
  input  G1,
  input  P1,
  input  G2,
  input  P2,
  input  G3,
  input  P3,
  input  C0,
  input  G4,
  input  P4,
  input  G5,
  input  P5,
  input  G6,
  input  P6,
  input  G7,
  input  P7,
  output C8
);

  wire cc_1bit_1_cout, cc_1bit_2_cout, cc_1bit_3_cout, cc_1bit_4_cout, cc_1bit_5_cout, cc_1bit_6_cout,
       cc_1bit_7_cout;

  cc_1bit cc_1bit_1 (.P(P0), .G(G0), .Cin(C0), .Cout(cc_1bit_1_cout));
  cc_1bit cc_1bit_2 (.P(P1), .G(G1), .Cin(cc_1bit_1_cout), .Cout(cc_1bit_2_cout));
  cc_1bit cc_1bit_3 (.P(P2), .G(G2), .Cin(cc_1bit_2_cout), .Cout(cc_1bit_3_cout));
  cc_1bit cc_1bit_4 (.P(P3), .G(G3), .Cin(cc_1bit_3_cout), .Cout(cc_1bit_4_cout));
  cc_1bit cc_1bit_5 (.P(P4), .G(G4), .Cin(cc_1bit_4_cout), .Cout(cc_1bit_5_cout));
  cc_1bit cc_1bit_6 (.P(P5), .G(G5), .Cin(cc_1bit_5_cout), .Cout(cc_1bit_6_cout));
  cc_1bit cc_1bit_7 (.P(P6), .G(G6), .Cin(cc_1bit_6_cout), .Cout(cc_1bit_7_cout));
  cc_1bit cc_1bit_8 (.P(P7), .G(G7), .Cin(cc_1bit_7_cout), .Cout(C8));
endmodule
