// Digital circuit comparateur 1bit.dig as structural Verilog
module comparateur_1bit (
  input  a,
  input  b,
  output gt,
  output eq,
  output lt
);

  wire not_1_out, not_2_out;

  not not_1 (not_1_out, a);
  not not_2 (not_2_out, b);
  and and_1 (gt, a, not_2_out);
  xnor xnor_1 (eq, a, b);
  and and_2 (lt, not_1_out, b);
endmodule
