// Digital circuit compteur modulo 8.dig as structural Verilog
module compteur_modulo_8 (
  input  Reset,
  input  w,
  output s0,
  output s1,
  output s2
);

  wire and_1_out, and_2_out, and_3_out, and_4_out, and_5_out, and_6_out, and_7_out, and_8_out, and_9_out,
       D0_nq, D1_nq, D2_nq, not_1_out, or_1_out, or_2_out, xor_1_out;

  not not_1 (not_1_out, Reset);
  and and_1 (and_1_out, s2, D0_nq);
  and and_2 (and_2_out, s2, D1_nq);
  and and_3 (and_3_out, s0, s1);
  and and_4 (and_4_out, D2_nq, not_1_out);
  and and_5 (and_5_out, and_1_out, not_1_out);
  and and_6 (and_6_out, and_2_out, not_1_out);
  and and_7 (and_7_out, and_3_out, and_4_out);
  or or_1 (or_1_out, and_5_out, and_6_out);
  or or_2 (or_2_out, or_1_out, and_7_out);
  D_FF D2 (.D(or_2_out), .C(w), .Q(s2), .nQ(D2_nq));
  xor xor_1 (xor_1_out, s0, s1);
  and and_8 (and_8_out, xor_1_out, not_1_out);
  D_FF D1 (.D(and_8_out), .C(w), .Q(s1), .nQ(D1_nq));
  and and_9 (and_9_out, not_1_out, D0_nq);
  D_FF D0 (.D(and_9_out), .C(w), .Q(s0), .nQ(D0_nq));
endmodule
