// Digital circuit registre_decalage_gauche_droite 8 bits.dig as structural Verilog
module registre_decalage_gauche_droite_8_bits (
  input  e0,
  input  dec,
  input  e1,
  input  e2,
  input  e3,
  input  e4,
  input  e5,
  input  e6,
  input  e7,
  input  CLK,
  input  left,
  output s0,
  output s1,
  output s2,
  output s3,
  output s4,
  output s5,
  output s6,
  output s7
);

  wire multiplexer_1_out, multiplexer_2_out, multiplexer_3_out, multiplexer_4_out, multiplexer_5_out,
       multiplexer_6_out, multiplexer_7_out, multiplexer_8_out, multiplexer_9_out, multiplexer_10_out,
       multiplexer_11_out, multiplexer_12_out, multiplexer_13_out, multiplexer_14_out, multiplexer_15_out,
       multiplexer_16_out;

  Multiplexer multiplexer_1 (.sel(dec), .in_0(e7), .in_1(1'b0), .out(multiplexer_1_out));
  Multiplexer multiplexer_2 (.sel(dec), .in_0(e6), .in_1(s7), .out(multiplexer_2_out));
  Multiplexer multiplexer_3 (.sel(dec), .in_0(e5), .in_1(s6), .out(multiplexer_3_out));
  Multiplexer multiplexer_4 (.sel(dec), .in_0(e4), .in_1(s5), .out(multiplexer_4_out));
  Multiplexer multiplexer_5 (.sel(dec), .in_0(e3), .in_1(s4), .out(multiplexer_5_out));
  Multiplexer multiplexer_6 (.sel(dec), .in_0(e2), .in_1(s3), .out(multiplexer_6_out));
  Multiplexer multiplexer_7 (.sel(dec), .in_0(e1), .in_1(s2), .out(multiplexer_7_out));
  Multiplexer multiplexer_8 (.sel(dec), .in_0(e0), .in_1(s1), .out(multiplexer_8_out));
  Multiplexer multiplexer_9 (.sel(left), .in_0(multiplexer_1_out), .in_1(s6), .out(multiplexer_9_out));
  Multiplexer multiplexer_10 (.sel(left), .in_0(multiplexer_2_out), .in_1(s5), .out(multiplexer_10_out));
  Multiplexer multiplexer_11 (.sel(left), .in_0(multiplexer_3_out), .in_1(s4), .out(multiplexer_11_out));
  Multiplexer multiplexer_12 (.sel(left), .in_0(multiplexer_4_out), .in_1(s3), .out(multiplexer_12_out));
  Multiplexer multiplexer_13 (.sel(left), .in_0(multiplexer_5_out), .in_1(s2), .out(multiplexer_13_out));
  Multiplexer multiplexer_14 (.sel(left), .in_0(multiplexer_6_out), .in_1(s1), .out(multiplexer_14_out));
  Multiplexer multiplexer_15 (.sel(left), .in_0(multiplexer_7_out), .in_1(s0), .out(multiplexer_15_out));
  Multiplexer multiplexer_16 (.sel(left), .in_0(multiplexer_8_out), .in_1(1'b0), .out(multiplexer_16_out));
  D_FF d_ff_1 (.D(multiplexer_9_out), .C(CLK), .Q(s7));  // open: nQ
  D_FF d_ff_2 (.D(multiplexer_10_out), .C(CLK), .Q(s6));  // open: nQ
  D_FF d_ff_3 (.D(multiplexer_11_out), .C(CLK), .Q(s5));  // open: nQ
  D_FF d_ff_4 (.D(multiplexer_12_out), .C(CLK), .Q(s4));  // open: nQ
  D_FF d_ff_5 (.D(multiplexer_13_out), .C(CLK), .Q(s3));  // open: nQ
  D_FF d_ff_6 (.D(multiplexer_14_out), .C(CLK), .Q(s2));  // open: nQ
  D_FF d_ff_7 (.D(multiplexer_15_out), .C(CLK), .Q(s1));  // open: nQ
  D_FF d_ff_8 (.D(multiplexer_16_out), .C(CLK), .Q(s0));  // open: nQ
endmodule
