// Digital circuit ADD_sub.dig as structural Verilog
module ADD_sub (
  input  S,
  input  [7:0] B,
  input  [7:0] A,
  output s0,
  output s1,
  output s2,
  output s3,
  output s4,
  output s5,
  output s6,
  output s7
);

  Add_sub_8bits add_sub_8bits_1 (
    .S(S), .b0(B[0]), .b1(B[1]), .b2(B[2]), .b3(B[3]), .b4(B[4]), .b5(B[5]), .b6(B[6]), .b7(B[7]), .a0(A[0]),
    .a1(A[1]), .a2(A[2]), .a3(A[3]), .a4(A[4]), .a5(A[5]), .a6(A[6]), .a7(A[7]), .s0(s0), .s1(s1), .s2(s2),
    .s3(s3), .s4(s4), .s5(s5), .s6(s6), .s7(s7));
endmodule
