// Digital circuit AND 8bits.dig as structural Verilog
module AND_8bits (
  input  a0,
  input  a1,
  input  a2,
  input  a3,
  input  a4,
  input  a5,
  input  a6,
  input  a7,
  input  b0,
  input  b1,
  input  b2,
  input  b3,
  input  b4,
  input  b5,
  input  b6,
  input  b7,
  output s0,
  output s1,
  output s2,
  output s3,
  output s4,
  output s5,
  output s6,
  output s7
);

  and and_1 (s7, a7, b7);
  and and_2 (s6, a6, b6);
  and and_3 (s5, a5, b5);
  and and_4 (s4, a4, b4);
  and and_5 (s3, a3, b3);
  and and_6 (s2, a2, b2);
  and and_7 (s1, a1, b1);
  and and_8 (s0, a0, b0);
endmodule
