// Digital circuit Add_sub 8bits.dig as structural Verilog
module Add_sub_8bits (
  input  S,
  input  b0,
  input  b1,
  input  b2,
  input  b3,
  input  b4,
  input  b5,
  input  b6,
  input  b7,
  input  a0,
  input  a1,
  input  a2,
  input  a3,
  input  a4,
  input  a5,
  input  a6,
  input  a7,
  output s0,
  output s1,
  output s2,
  output s3,
  output s4,
  output s5,
  output s6,
  output s7
);

  wire add_1_c_o, add_2_c_o, add_3_c_o, add_4_c_o, add_5_c_o, add_6_c_o, add_7_c_o, add_8_c_o, xor_1_out,
       xor_2_out, xor_3_out, xor_4_out, xor_5_out, xor_6_out, xor_7_out, xor_8_out;

  xor xor_1 (xor_1_out, S, b7);
  Add add_1 (.a(a7), .b(xor_1_out), .c_i(add_2_c_o), .s(s7), .c_o(add_1_c_o));
  xor xor_2 (xor_2_out, S, b6);
  Add add_2 (.a(a6), .b(xor_2_out), .c_i(add_3_c_o), .s(s6), .c_o(add_2_c_o));
  xor xor_3 (xor_3_out, S, b5);
  Add add_3 (.a(a5), .b(xor_3_out), .c_i(add_4_c_o), .s(s5), .c_o(add_3_c_o));
  xor xor_4 (xor_4_out, S, b4);
  Add add_4 (.a(a4), .b(xor_4_out), .c_i(add_5_c_o), .s(s4), .c_o(add_4_c_o));
  xor xor_5 (xor_5_out, S, b3);
  Add add_5 (.a(a3), .b(xor_5_out), .c_i(add_6_c_o), .s(s3), .c_o(add_5_c_o));
  xor xor_6 (xor_6_out, S, b2);
  Add add_6 (.a(a2), .b(xor_6_out), .c_i(add_7_c_o), .s(s2), .c_o(add_6_c_o));
  xor xor_7 (xor_7_out, S, b1);
  Add add_7 (.a(a1), .b(xor_7_out), .c_i(add_8_c_o), .s(s1), .c_o(add_7_c_o));
  xor xor_8 (xor_8_out, S, b0);
  Add add_8 (.a(a0), .b(xor_8_out), .c_i(S), .s(s0), .c_o(add_8_c_o));
endmodule
