// Digital circuit Adder 8bits.dig as structural Verilog
module Adder_8bits (
  input  a0,
  input  b0,
  input  Cin,
  input  a1,
  input  b1,
  input  a2,
  input  b2,
  input  a3,
  input  b3,
  input  a4,
  input  b4,
  input  a5,
  input  b5,
  input  a6,
  input  b6,
  input  a7,
  input  b7,
  output Cout
);

  wire full_adder_2_s, full_adder_3_s, full_adder_4_s, full_adder_5_s, full_adder_6_s, full_adder_7_s,
       full_adder_8_s;

  full_adder full_adder_1 (.a(a7), .b(b7), .Cin(full_adder_2_s), .s(Cout));  // open: Cout
  full_adder full_adder_2 (.a(a6), .b(b6), .Cin(full_adder_3_s), .s(full_adder_2_s));  // open: Cout
  full_adder full_adder_3 (.a(a5), .b(b5), .Cin(full_adder_4_s), .s(full_adder_3_s));  // open: Cout
  full_adder full_adder_4 (.a(a4), .b(b4), .Cin(full_adder_5_s), .s(full_adder_4_s));  // open: Cout
  full_adder full_adder_5 (.a(a3), .b(b3), .Cin(full_adder_6_s), .s(full_adder_5_s));  // open: Cout
  full_adder full_adder_6 (.a(a2), .b(b2), .Cin(full_adder_7_s), .s(full_adder_6_s));  // open: Cout
  full_adder full_adder_7 (.a(a1), .b(b1), .Cin(full_adder_8_s), .s(full_adder_7_s));  // open: Cout
  full_adder full_adder_8 (.a(a0), .b(b0), .Cin(Cin), .s(full_adder_8_s));  // open: Cout
endmodule
