// Digital circuit MUX 4 vers 1.dig as structural Verilog
module MUX_4_vers_1 (
  input  [7:0] A,
  input  [7:0] B,
  input  [7:0] C,
  input  [7:0] D,
  input  C1,
  input  C2,
  output [7:0] S
);

  wire and_1_out, and_2_out, and_3_out, and_4_out, and_5_out, and_6_out, and_7_out, and_8_out, and_9_out,
       and_10_out, and_11_out, and_12_out, and_13_out, and_14_out, and_15_out, and_16_out, and_17_out,
       and_18_out, and_19_out, and_20_out, and_21_out, and_22_out, and_23_out, and_24_out, and_25_out,
       and_26_out, and_27_out, and_28_out, and_29_out, and_30_out, and_31_out, and_32_out, and_33_out,
       and_34_out, and_35_out, and_36_out, and_37_out, and_38_out, and_39_out, and_40_out, and_41_out,
       and_42_out, and_43_out, and_44_out, and_45_out, and_46_out, and_47_out, and_48_out, and_49_out,
       and_50_out, and_51_out, and_52_out, and_53_out, and_54_out, and_55_out, and_56_out, and_57_out,
       and_58_out, and_59_out, and_60_out, and_61_out, and_62_out, and_63_out, and_64_out, not_1_out,
       not_2_out, or_1_out, or_2_out, or_3_out, or_4_out, or_5_out, or_6_out, or_7_out, or_8_out, or_9_out,
       or_10_out, or_11_out, or_12_out, or_13_out, or_14_out, or_15_out, or_16_out;

  not not_1 (not_1_out, C1);
  not not_2 (not_2_out, C2);
  and and_1 (and_1_out, not_1_out, not_2_out);
  and and_2 (and_2_out, C1, not_2_out);
  and and_3 (and_3_out, not_1_out, C2);
  and and_4 (and_4_out, C2, C1);
  and and_5 (and_5_out, not_1_out, not_2_out);
  and and_6 (and_6_out, C1, not_2_out);
  and and_7 (and_7_out, not_1_out, C2);
  and and_8 (and_8_out, C2, C1);
  and and_9 (and_9_out, not_1_out, not_2_out);
  and and_10 (and_10_out, C1, not_2_out);
  and and_11 (and_11_out, not_1_out, C2);
  and and_12 (and_12_out, C2, C1);
  and and_13 (and_13_out, not_1_out, not_2_out);
  and and_14 (and_14_out, C1, not_2_out);
  and and_15 (and_15_out, not_1_out, C2);
  and and_16 (and_16_out, C2, C1);
  and and_17 (and_17_out, not_1_out, not_2_out);
  and and_18 (and_18_out, C1, not_2_out);
  and and_19 (and_19_out, not_1_out, C2);
  and and_20 (and_20_out, C2, C1);
  and and_21 (and_21_out, not_1_out, not_2_out);
  and and_22 (and_22_out, C1, not_2_out);
  and and_23 (and_23_out, not_1_out, C2);
  and and_24 (and_24_out, C2, C1);
  and and_25 (and_25_out, not_1_out, not_2_out);
  and and_26 (and_26_out, C1, not_2_out);
  and and_27 (and_27_out, not_1_out, C2);
  and and_28 (and_28_out, C2, C1);
  and and_29 (and_29_out, not_1_out, not_2_out);
  and and_30 (and_30_out, C1, not_2_out);
  and and_31 (and_31_out, not_1_out, C2);
  and and_32 (and_32_out, C2, C1);
  and and_33 (and_33_out, A[0], and_1_out);
  and and_34 (and_34_out, B[0], and_2_out);
  and and_35 (and_35_out, C[1], and_3_out);
  and and_36 (and_36_out, D[0], and_4_out);
  and and_37 (and_37_out, A[1], and_5_out);
  and and_38 (and_38_out, B[1], and_6_out);
  and and_39 (and_39_out, C[0], and_7_out);
  and and_40 (and_40_out, D[1], and_8_out);
  and and_41 (and_41_out, A[2], and_9_out);
  and and_42 (and_42_out, B[2], and_10_out);
  and and_43 (and_43_out, C[2], and_11_out);
  and and_44 (and_44_out, D[2], and_12_out);
  and and_45 (and_45_out, A[3], and_13_out);
  and and_46 (and_46_out, B[3], and_14_out);
  and and_47 (and_47_out, C[3], and_15_out);
  and and_48 (and_48_out, D[3], and_16_out);
  and and_49 (and_49_out, A[4], and_17_out);
  and and_50 (and_50_out, B[4], and_18_out);
  and and_51 (and_51_out, C[4], and_19_out);
  and and_52 (and_52_out, D[4], and_20_out);
  and and_53 (and_53_out, A[5], and_21_out);
  and and_54 (and_54_out, B[5], and_22_out);
  and and_55 (and_55_out, C[5], and_23_out);
  and and_56 (and_56_out, D[5], and_24_out);
  and and_57 (and_57_out, A[6], and_25_out);
  and and_58 (and_58_out, B[6], and_26_out);
  and and_59 (and_59_out, C[6], and_27_out);
  and and_60 (and_60_out, D[6], and_28_out);
  and and_61 (and_61_out, A[7], and_29_out);
  and and_62 (and_62_out, B[7], and_30_out);
  and and_63 (and_63_out, C[7], and_31_out);
  and and_64 (and_64_out, D[7], and_32_out);
  or or_1 (or_1_out, and_33_out, and_34_out);
  or or_2 (or_2_out, and_35_out, and_36_out);
  or or_3 (or_3_out, and_37_out, and_38_out);
  or or_4 (or_4_out, and_39_out, and_40_out);
  or or_5 (or_5_out, and_41_out, and_42_out);
  or or_6 (or_6_out, and_43_out, and_44_out);
  or or_7 (or_7_out, and_45_out, and_46_out);
  or or_8 (or_8_out, and_47_out, and_48_out);
  or or_9 (or_9_out, and_49_out, and_50_out);
  or or_10 (or_10_out, and_51_out, and_52_out);
  or or_11 (or_11_out, and_53_out, and_54_out);
  or or_12 (or_12_out, and_55_out, and_56_out);
  or or_13 (or_13_out, and_57_out, and_58_out);
  or or_14 (or_14_out, and_59_out, and_60_out);
  or or_15 (or_15_out, and_61_out, and_62_out);
  or or_16 (or_16_out, and_63_out, and_64_out);
  or or_17 (S[0], or_1_out, or_2_out);
  or or_18 (S[1], or_3_out, or_4_out);
  or or_19 (S[2], or_5_out, or_6_out);
  or or_20 (S[3], or_7_out, or_8_out);
  or or_21 (S[4], or_9_out, or_10_out);
  or or_22 (S[5], or_11_out, or_12_out);
  or or_23 (S[6], or_13_out, or_14_out);
  or or_24 (S[7], or_15_out, or_16_out);
endmodule
