// Digital circuit Mux 8 entrées (non récursif).dig as structural Verilog
module \Mux_8_entrées__non_récursif  (
  input  e0,
  input  [2:0] S,
  input  e1,
  input  e2,
  input  e3,
  input  e4,
  input  e5,
  input  e6,
  input  e7,
  output Y
);

  Multiplexer #(.Selector_Bits(3)) multiplexer_1 (
    .sel(S), .in_0(e0), .in_1(e1), .in_2(e2), .in_3(e3), .in_4(e4), .in_5(e5), .in_6(e6), .in_7(e7), .out(Y));
endmodule
