// Digital circuit Mux 8 entrées (récursif1).dig as structural Verilog
module \Mux_8_entrées__récursif1  (
  input  s2,
  input  e0,
  input  s1,
  input  s0,
  input  e1,
  input  e2,
  input  e3,
  input  e4,
  input  e5,
  input  e6,
  input  e7,
  output y
);

  wire \mux_2_entrées_1_y , \mux_2_entrées_2_y , \mux_2_entrées_3_y , \mux_2_entrées_4_y ,
       \mux_2_entrées_5_y , \mux_2_entrées_6_y ;

  \Mux_2_entrées  \mux_2_entrées_1  (.a(e7), .b(e6), .s(s0), .y(\mux_2_entrées_1_y ));
  \Mux_2_entrées  \mux_2_entrées_2  (.a(e5), .b(e4), .s(s0), .y(\mux_2_entrées_2_y ));
  \Mux_2_entrées  \mux_2_entrées_3  (.a(e3), .b(e2), .s(s0), .y(\mux_2_entrées_3_y ));
  \Mux_2_entrées  \mux_2_entrées_4  (.a(e1), .b(e0), .s(s0), .y(\mux_2_entrées_4_y ));
  \Mux_2_entrées  \mux_2_entrées_5  (.a(\mux_2_entrées_1_y ), .b(\mux_2_entrées_2_y ), .s(s1), .y(\mux_2_entrées_5_y ));
  \Mux_2_entrées  \mux_2_entrées_6  (.a(\mux_2_entrées_3_y ), .b(\mux_2_entrées_4_y ), .s(s1), .y(\mux_2_entrées_6_y ));
  \Mux_2_entrées  \mux_2_entrées_7  (.a(\mux_2_entrées_5_y ), .b(\mux_2_entrées_6_y ), .s(s2), .y(y));
endmodule
