// Digital circuit UAL.dig as structural Verilog
module UAL (
  input  [7:0] A,
  input  [7:0] B,
  input  S,
  input  C0,
  input  C1,
  output [7:0] S_2
);

  wire [7:0] add_sub_1_s7, circuit_and_1_s7, circuit_or_1_s7, xor_8bits_1_s5;

  XOR_8bits xor_8bits_1 (
    .A(A), .B(B), .s0(xor_8bits_1_s5[0]), .s1(xor_8bits_1_s5[1]), .s2(xor_8bits_1_s5[2]),
    .s3(xor_8bits_1_s5[3]), .s4(xor_8bits_1_s5[4]), .s5(xor_8bits_1_s5[5]), .s6(xor_8bits_1_s5[6]),
    .s7(xor_8bits_1_s5[7]));
  Circuit_OR circuit_or_1 (
    .A(A), .B(B), .s0(circuit_or_1_s7[0]), .s1(circuit_or_1_s7[1]), .s2(circuit_or_1_s7[2]),
    .s3(circuit_or_1_s7[3]), .s4(circuit_or_1_s7[4]), .s5(circuit_or_1_s7[5]), .s6(circuit_or_1_s7[6]),
    .s7(circuit_or_1_s7[7]));
  MUX_4_vers_1 mux_4_vers_1_1 (
    .A(add_sub_1_s7), .B(circuit_and_1_s7), .C(circuit_or_1_s7), .D(xor_8bits_1_s5), .C1(C0), .C2(C1), .S(S_2));
  Circuit_AND circuit_and_1 (
    .A(A), .B(B), .s0(circuit_and_1_s7[0]), .s1(circuit_and_1_s7[1]), .s2(circuit_and_1_s7[2]),
    .s3(circuit_and_1_s7[3]), .s4(circuit_and_1_s7[4]), .s5(circuit_and_1_s7[5]), .s6(circuit_and_1_s7[6]),
    .s7(circuit_and_1_s7[7]));
  ADD_sub add_sub_1 (
    .S(S), .B(B), .A(A), .s0(add_sub_1_s7[0]), .s1(add_sub_1_s7[1]), .s2(add_sub_1_s7[2]),
    .s3(add_sub_1_s7[3]), .s4(add_sub_1_s7[4]), .s5(add_sub_1_s7[5]), .s6(add_sub_1_s7[6]),
    .s7(add_sub_1_s7[7]));
endmodule
