// Digital circuit XOR.dig as structural Verilog
module XOR (
  input  a0,
  input  a1,
  input  a2,
  input  a3,
  input  a4,
  input  a5,
  input  a6,
  input  a7,
  input  b0,
  input  b1,
  input  b2,
  input  b3,
  input  b4,
  input  b5,
  input  b6,
  input  b7,
  output s0,
  output s1,
  output s2,
  output s3,
  output s4,
  output s5,
  output s6,
  output s7
);

  xor xor_1 (s7, a7, b7);
  xor xor_2 (s6, a6, b6);
  xor xor_3 (s5, a5, b5);
  xor xor_4 (s4, a4, b4);
  xor xor_5 (s3, a3, b3);
  xor xor_6 (s2, a2, b2);
  xor xor_7 (s1, a1, b1);
  xor xor_8 (s0, a0, b0);
endmodule
