// Digital circuit barrel shifter 1 bit.dig as structural Verilog
module barrel_shifter_1_bit (
  input  e0,
  input  e1,
  input  e2,
  input  e3,
  input  e4,
  input  e5,
  input  e6,
  input  e7,
  input  d0,
  output s0,
  output s1,
  output s2,
  output s3,
  output s4,
  output s5,
  output s6,
  output s7
);

  Multiplexer multiplexer_1 (.sel(d0), .in_0(e7), .in_1(e6), .out(s7));
  Multiplexer multiplexer_2 (.sel(d0), .in_0(e6), .in_1(e5), .out(s6));
  Multiplexer multiplexer_3 (.sel(d0), .in_0(e5), .in_1(e4), .out(s5));
  Multiplexer multiplexer_4 (.sel(d0), .in_0(e4), .in_1(e3), .out(s4));
  Multiplexer multiplexer_5 (.sel(d0), .in_0(e3), .in_1(e2), .out(s3));
  Multiplexer multiplexer_6 (.sel(d0), .in_0(e2), .in_1(e1), .out(s2));
  Multiplexer multiplexer_7 (.sel(d0), .in_0(e1), .in_1(e0), .out(s1));
  Multiplexer multiplexer_8 (.sel(d0), .in_0(e0), .in_1(1'b0), .out(s0));
endmodule
