// Digital circuit barrel shifter 2 bits.dig as structural Verilog
module barrel_shifter_2_bits (
  input  e0,
  input  e1,
  input  e2,
  input  e3,
  input  e4,
  input  e5,
  input  e6,
  input  e7,
  input  d0,
  input  d1,
  output s0,
  output s1,
  output s2,
  output s3,
  output s4,
  output s5,
  output s6,
  output s7
);

  wire multiplexer_1_out, multiplexer_3_out, multiplexer_6_out, multiplexer_7_out, multiplexer_9_out,
       multiplexer_11_out, multiplexer_13_out, multiplexer_16_out;

  Multiplexer multiplexer_1 (.sel(d0), .in_0(e7), .in_1(e6), .out(multiplexer_1_out));
  Multiplexer multiplexer_2 (.sel(d1), .in_0(multiplexer_1_out), .in_1(multiplexer_6_out), .out(s7));
  Multiplexer multiplexer_3 (.sel(d0), .in_0(e6), .in_1(e5), .out(multiplexer_3_out));
  Multiplexer multiplexer_4 (.sel(d1), .in_0(multiplexer_3_out), .in_1(multiplexer_7_out), .out(s6));
  Multiplexer multiplexer_5 (.sel(d1), .in_0(multiplexer_6_out), .in_1(multiplexer_9_out), .out(s5));
  Multiplexer multiplexer_6 (.sel(d0), .in_0(e5), .in_1(e4), .out(multiplexer_6_out));
  Multiplexer multiplexer_7 (.sel(d0), .in_0(e4), .in_1(e3), .out(multiplexer_7_out));
  Multiplexer multiplexer_8 (.sel(d1), .in_0(multiplexer_7_out), .in_1(multiplexer_11_out), .out(s4));
  Multiplexer multiplexer_9 (.sel(d0), .in_0(e3), .in_1(e2), .out(multiplexer_9_out));
  Multiplexer multiplexer_10 (.sel(d1), .in_0(multiplexer_9_out), .in_1(multiplexer_13_out), .out(s3));
  Multiplexer multiplexer_11 (.sel(d0), .in_0(e2), .in_1(e1), .out(multiplexer_11_out));
  Multiplexer multiplexer_12 (.sel(d1), .in_0(multiplexer_11_out), .in_1(multiplexer_16_out), .out(s2));
  Multiplexer multiplexer_13 (.sel(d0), .in_0(e1), .in_1(e0), .out(multiplexer_13_out));
  Multiplexer multiplexer_14 (.sel(d1), .in_0(multiplexer_13_out), .in_1(1'b0), .out(s1));
  Multiplexer multiplexer_15 (.sel(d1), .in_0(multiplexer_16_out), .in_1(1'b0), .out(s0));
  Multiplexer multiplexer_16 (.sel(d0), .in_0(e0), .in_1(1'b0), .out(multiplexer_16_out));
endmodule
