// Digital circuit Compteur modulo 4.dig as structural Verilog
module Compteur_modulo_4 (
  input  CLK,
  output Q0,
  output Q1
);

  wire d_ff_1_nq, xor_1_out;

  D_FF d_ff_1 (.D(d_ff_1_nq), .C(CLK), .Q(Q0), .nQ(d_ff_1_nq));
  xor xor_1 (xor_1_out, Q1, Q0);
  D_FF d_ff_2 (.D(xor_1_out), .C(CLK), .Q(Q1));  // open: nQ
endmodule
