// Digital circuit Compteur modulo 8.dig as structural Verilog
module Compteur_modulo_8 (
  input  CLK,
  output Q0,
  output Q1,
  output Q2
);

  wire and_1_out, and_2_out, D0_nq, D1_nq, or_1_out, xor_1_out, xor_2_out;

  xor xor_1 (xor_1_out, Q0, Q2);
  and and_1 (and_1_out, Q2, D1_nq);
  and and_2 (and_2_out, Q1, xor_1_out);
  or or_1 (or_1_out, and_2_out, and_1_out);
  D_FF D2 (.D(or_1_out), .C(CLK), .Q(Q2));  // open: nQ
  xor xor_2 (xor_2_out, Q0, Q1);
  D_FF D1 (.D(xor_2_out), .C(CLK), .Q(Q1), .nQ(D1_nq));
  D_FF D0 (.D(D0_nq), .C(CLK), .Q(Q0), .nQ(D0_nq));
endmodule
