// Digital circuit Compteur.dig as structural Verilog
module Compteur (
  input  w,
  input  reset,
  output S0,
  output S1,
  output S2
);

  wire and_1_out, and_2_out, and_3_out, and_4_out, and_5_out, D0_nq, D1_nq, not_1_out, or_1_out, xor_1_out,
       xor_2_out;

  and and_1 (and_1_out, S2, D1_nq);
  xor xor_1 (xor_1_out, S0, S2);
  and and_2 (and_2_out, S1, xor_1_out);
  or or_1 (or_1_out, and_1_out, and_2_out);
  not not_1 (not_1_out, reset);
  and and_3 (and_3_out, not_1_out, or_1_out);
  D_FF D2 (.D(and_3_out), .C(w), .Q(S2));  // open: nQ
  xor xor_2 (xor_2_out, S1, S0);
  and and_4 (and_4_out, not_1_out, xor_2_out);
  D_FF D1 (.D(and_4_out), .C(w), .Q(S1), .nQ(D1_nq));
  and and_5 (and_5_out, not_1_out, D0_nq);
  D_FF D0 (.D(and_5_out), .C(w), .Q(S0), .nQ(D0_nq));
endmodule
