// Digital circuit compt_dcmpt_saturation.dig as structural Verilog
module compt_dcmpt_saturation (
  input  w,
  input  inc,
  input  res,
  output S0,
  output S1,
  output S2
);

  wire and_1_out, and_2_out, and_3_out, and_4_out, and_5_out, and_6_out, and_7_out, and_8_out, and_9_out,
       and_10_out, and_11_out, and_12_out, and_13_out, and_14_out, and_15_out, and_16_out, and_17_out,
       and_18_out, and_19_out, and_20_out, and_21_out, and_22_out, and_23_out, and_24_out, and_25_out,
       and_26_out, and_27_out, and_28_out, and_29_out, and_30_out, D0_nq, D1_nq, D2_nq, not_1_out, not_2_out,
       or_1_out, or_2_out, or_3_out, or_4_out, or_5_out, or_6_out, or_7_out, or_8_out, or_9_out;

  or or_1 (or_1_out, or_4_out, or_3_out);
  or or_2 (or_2_out, or_6_out, or_5_out);
  D_FF D2 (.D(or_1_out), .C(w), .Q(S2), .nQ(D2_nq));
  or or_3 (or_3_out, and_2_out, and_1_out);
  or or_4 (or_4_out, and_4_out, and_3_out);
  or or_5 (or_5_out, and_12_out, and_5_out);
  or or_6 (or_6_out, and_14_out, and_13_out);
  and and_1 (and_1_out, and_7_out, and_6_out);
  and and_2 (and_2_out, and_8_out, S1);
  and and_3 (and_3_out, and_9_out, S0);
  and and_4 (and_4_out, and_10_out, S2);
  and and_5 (and_5_out, and_11_out, S0);
  and and_6 (and_6_out, S1, S0);
  and and_7 (and_7_out, not_2_out, inc);
  and and_8 (and_8_out, not_2_out, S2);
  and and_9 (and_9_out, not_2_out, S2);
  and and_10 (and_10_out, not_2_out, inc);
  and and_11 (and_11_out, and_16_out, and_15_out);
  and and_12 (and_12_out, and_18_out, and_17_out);
  and and_13 (and_13_out, and_20_out, and_19_out);
  and and_14 (and_14_out, and_21_out, S1);
  or or_7 (or_7_out, or_9_out, or_8_out);
  or or_8 (or_8_out, and_23_out, and_22_out);
  or or_9 (or_9_out, and_25_out, and_24_out);
  and and_15 (and_15_out, D2_nq, D1_nq);
  and and_16 (and_16_out, not_2_out, not_1_out);
  and and_17 (and_17_out, S2, D0_nq);
  and and_18 (and_18_out, not_2_out, not_1_out);
  and and_19 (and_19_out, D2_nq, D0_nq);
  and and_20 (and_20_out, not_2_out, inc);
  and and_21 (and_21_out, not_2_out, inc);
  D_FF D1 (.D(or_2_out), .C(w), .Q(S1), .nQ(D1_nq));
  and and_22 (and_22_out, and_26_out, D0_nq);
  and and_23 (and_23_out, and_27_out, D0_nq);
  and and_24 (and_24_out, and_29_out, and_28_out);
  and and_25 (and_25_out, and_30_out, D0_nq);
  and and_26 (and_26_out, not_2_out, S1);
  and and_27 (and_27_out, not_2_out, S2);
  and and_28 (and_28_out, S2, S1);
  and and_29 (and_29_out, not_2_out, inc);
  and and_30 (and_30_out, not_2_out, inc);
  not not_1 (not_1_out, inc);
  D_FF D0 (.D(or_7_out), .C(w), .Q(S0), .nQ(D0_nq));
  not not_2 (not_2_out, res);
endmodule
