// Digital circuit compteur décomptur1.dig as structural Verilog
module \compteur_décomptur1  (
  input  w,
  input  inc,
  input  res,
  output S0,
  output S1,
  output S2
);

  wire and_1_out, and_2_out, and_3_out, and_4_out, and_5_out, and_6_out, and_7_out, and_8_out, and_9_out,
       and_10_out, and_11_out, D0_nq, D0_q, D1_nq, D1_q, D2_nq, D2_q, not_1_out, not_2_out, or_1_out,
       or_2_out, or_3_out, or_4_out, xnor_1_out, xor_1_out;

  not not_1 (not_1_out, res);
  not not_2 (not_2_out, inc);
  // And and_1 has open pins: In_1=open, In_2=open, out=and_1_out
  // And and_2 has open pins: In_1=open, In_2=open, out=and_2_out
  or or_1 (or_1_out, and_1_out, and_2_out);
  and and_3 (and_3_out, not_1_out, D2_q);
  and and_4 (and_4_out, D1_q, D0_nq);
  and and_5 (and_5_out, and_3_out, and_4_out);
  or or_2 (or_2_out, or_1_out, and_5_out);
  D_FF D2 (.D(or_2_out), .C(w), .Q(D2_q), .nQ(D2_nq));
  and and_6 (and_6_out, not_1_out, not_2_out);
  xnor xnor_1 (xnor_1_out, D0_q, D1_q);
  and and_7 (and_7_out, not_1_out, inc);
  xor xor_1 (xor_1_out, D0_q, D1_q);
  and and_8 (and_8_out, and_6_out, xnor_1_out);
  and and_9 (and_9_out, and_7_out, xor_1_out);
  or or_3 (or_3_out, and_8_out, and_9_out);
  D_FF D1 (.D(or_3_out), .C(w), .Q(D1_q), .nQ(D1_nq));
  and and_10 (and_10_out, D1_nq, D0_nq);
  or or_4 (or_4_out, D1_q, and_10_out);
  and and_11 (and_11_out, not_1_out, or_4_out);
  D_FF D0 (.D(and_11_out), .C(w), .Q(D0_q), .nQ(D0_nq));
endmodule
