// Digital circuit test.dig as structural Verilog
module test (
  input  CLK,
  output S0,
  output S1,
  output S2
);

  wire D0_nq, D1_nq, D2_nq;

  D_FF D2 (.D(D2_nq), .C(D1_nq), .Q(S2), .nQ(D2_nq));
  D_FF D1 (.D(D1_nq), .C(D0_nq), .Q(S1), .nQ(D1_nq));
  D_FF D0 (.D(D0_nq), .C(CLK), .Q(S0), .nQ(D0_nq));
endmodule
