// Digital circuit test_cmpt_dcmpt.dig as structural Verilog
module test_cmpt_dcmpt (
  input  w,
  input  inc,
  output S0,
  output S1,
  output S2
);

  wire and_1_out, and_2_out, and_3_out, and_4_out, and_5_out, and_6_out, and_7_out, D0_nq, D1_nq, D2_nq,
       not_1_out, or_1_out, or_2_out;

  not not_1 (not_1_out, inc);
  and and_1 (and_1_out, inc, S0);
  and and_2 (and_2_out, S1, D2_nq);
  and and_3 (and_3_out, S2, not_1_out);
  and and_4 (and_4_out, and_1_out, and_2_out);
  or or_1 (or_1_out, and_3_out, and_4_out);
  D_FF D2 (.D(or_1_out), .C(w), .Q(S2), .nQ(D2_nq));
  and and_5 (and_5_out, inc, S0);
  and and_6 (and_6_out, not_1_out, D1_nq);
  and and_7 (and_7_out, and_5_out, D1_nq);
  or or_2 (or_2_out, and_6_out, and_7_out);
  D_FF D1 (.D(or_2_out), .C(w), .Q(S1), .nQ(D1_nq));
  D_FF D0 (.D(D0_nq), .C(w), .Q(S0), .nQ(D0_nq));
endmodule
