// Digital circuit BRANCH.dig as structural Verilog
module BRANCH (
  input  [31:0] RES,
  input  [2:0] funct3,
  output Taken
);

  wire and_1_out, and_2_out, and_3_out, and_4_out, decoder_1_out_0, decoder_1_out_1, decoder_1_out_3,
       decoder_1_out_4, not_1_out, not_2_out, or_1_out, or_2_out, or_3_out, or_4_out, or_5_out, or_6_out,
       or_7_out, or_8_out, or_9_out, or_10_out, or_11_out;

  or or_1 (or_1_out, RES[0], RES[1], RES[2], RES[3]);
  or or_2 (or_2_out, RES[4], RES[5], RES[6], RES[7]);
  or or_3 (or_3_out, RES[8], RES[9], RES[10], RES[11]);
  or or_4 (or_4_out, RES[12], RES[13], RES[14], RES[15]);
  or or_5 (or_5_out, RES[16], RES[17], RES[18], RES[19]);
  or or_6 (or_6_out, RES[20], RES[21], RES[22], RES[23]);
  or or_7 (or_7_out, RES[24], RES[25], RES[26], RES[27]);
  or or_8 (or_8_out, RES[28], RES[29], RES[30], RES[31]);
  or or_9 (or_9_out, or_1_out, or_2_out, or_3_out, or_4_out);
  or or_10 (or_10_out, or_5_out, or_6_out, or_7_out, or_8_out);
  or or_11 (or_11_out, or_9_out, or_10_out);
  Decoder #(.Selector_Bits(3)) decoder_1 (
    .sel(funct3), .out_0(decoder_1_out_0), .out_1(decoder_1_out_1), .out_3(decoder_1_out_3),
    .out_4(decoder_1_out_4));  // open: out_2, out_5, out_6, out_7
  not not_1 (not_1_out, or_11_out);
  not not_2 (not_2_out, RES[31]);
  and and_1 (and_1_out, decoder_1_out_0, not_1_out);
  and and_2 (and_2_out, decoder_1_out_1, or_11_out);
  and and_3 (and_3_out, RES[31], decoder_1_out_3);
  and and_4 (and_4_out, not_2_out, decoder_1_out_4);
  or or_12 (Taken, and_1_out, and_2_out, and_3_out, and_4_out);

  // Notes on the sheet:
  //   BEQ
  //   BNE
  //   BLT
  //   BGE
endmodule
