// Digital circuit Data_Path_1.3.dig as structural Verilog
module Data_Path_1_3 (
  input  W_IR,
  input  W_PC,
  input  G_PC,
  input  W_RES,
  input  SUB,
  input  MUX_ALU,
  input  G_ALU,
  input  W_MAR,
  input  W_MDR,
  input  MUX_MDR,
  input  G_MDR,
  input  W_MDR_2,
  input  G_RS2,
  input  MUX_IM,
  input  MUX_FCT3,
  input  MUX_PC
);

  wire not_1_out;
  wire [2:0] multiplexer_5_out;
  wire [11:0] multiplexer_2_out;
  wire [31:0] add_1_s, banc_de_registres_1_src1, banc_de_registres_1_src2, bitextender_1_out,
       bitextender_2_out, branch_1_p1, driver_1_out, IR_q, MAR_q, MDR_q, multiplexer_1_out,
       multiplexer_3_out, multiplexer_4_out, PC_q, ramsingleportsel_1_d;

  Register #(.Bits(32)) PC (.D(add_1_s), .C(W_PC), .en(W_PC), .Q(PC_q));
  Add #(.Bits(32)) add_1 (.a(multiplexer_1_out), .b(PC_q), .c_i(1'b0), .s(add_1_s));  // open: c_o
  Register #(.Bits(32)) IR (.D(driver_1_out), .C(W_IR), .en(W_IR), .Q(IR_q));
  Multiplexer #(.Bits(32)) multiplexer_1 (
    .sel(MUX_PC), .in_0(32'h4), .in_1(bitextender_1_out), .out(multiplexer_1_out));
  assign driver_1_out = G_PC ? PC_q : 32'bz;  // Driver driver_1
  BitExtender #(.inputBits(12), .outputBits(32)) bitextender_1 (
    .in({IR_q[25], IR_q[7], IR_q[31:26], IR_q[11:8]}), .out(bitextender_1_out));
  Multiplexer #(.Bits(12)) multiplexer_2 (
    .sel(MUX_IM), .in_0(IR_q[31:20]), .in_1({IR_q[31:25], IR_q[11:7]}), .out(multiplexer_2_out));
  BitExtender #(.inputBits(12), .outputBits(32)) bitextender_2 (.in(multiplexer_2_out), .out(bitextender_2_out));
  Register #(.Bits(32)) MAR (.D(driver_1_out), .C(W_MAR), .en(W_MAR), .Q(MAR_q));
  Banc_De_Registres banc_de_registres_1 (
    .Wreg(W_RES), .rd(IR_q[11:7]), .rs1(IR_q[19:15]), .rs2(IR_q[24:20]), .res(driver_1_out),
    .src1(banc_de_registres_1_src1), .src2(banc_de_registres_1_src2));  // open: x5, x6, x7
  not not_1 (not_1_out, W_MDR_2);
  RAMSinglePortSel #(.AddrBits(8), .Bits(32)) ramsingleportsel_1 (
    .A(MAR_q[9:2]), .CS(1'b1), .WE(W_MDR_2), .OE(not_1_out), .D(ramsingleportsel_1_d));
  assign driver_1_out = G_RS2 ? banc_de_registres_1_src2 : 32'bz;  // Driver driver_2
  Multiplexer #(.Bits(32)) multiplexer_3 (
    .sel(MUX_ALU), .in_0(banc_de_registres_1_src2), .in_1(bitextender_2_out), .out(multiplexer_3_out));
  Multiplexer #(.Bits(32)) multiplexer_4 (
    .sel(MUX_MDR), .in_0(ramsingleportsel_1_d), .in_1(driver_1_out), .out(multiplexer_4_out));
  // BRANCH branch_1: pin names not known; wires that end beside it: branch_1_p1, IR_q[14:12]
  Register #(.Bits(32)) MDR (.D(multiplexer_4_out), .C(W_MDR), .en(W_MDR), .Q(MDR_q));
  Multiplexer #(.Bits(3)) multiplexer_5 (.sel(MUX_FCT3), .in_0(IR_q[14:12]), .in_1(3'b000), .out(multiplexer_5_out));
  assign ramsingleportsel_1_d = W_MDR_2 ? MDR_q : 32'bz;  // Driver driver_3
  // UAL__1 ual__1_1: pin names not known; wires that end beside it: SUB, multiplexer_5_out, banc_de_registres_1_src1, multiplexer_3_out, branch_1_p1
  assign driver_1_out = G_MDR ? MDR_q : 32'bz;  // Driver driver_4
  assign driver_1_out = G_ALU ? branch_1_p1 : 32'bz;  // Driver driver_5
endmodule
