// Digital circuit Data_Path_1.4.dig as structural Verilog
module Data_Path_1_4 (
  input  W_IR,
  input  W_PC,
  input  G_PC,
  input  W_RES,
  input  SUB,
  input  MUX_ALU,
  input  G_ALU,
  input  W_MAR,
  input  W_MDR,
  input  MUX_MDR,
  input  G_MDR,
  input  W_MDR_2,
  input  G_RS2,
  input  MUX_IM,
  input  MUX_FCT3,
  input  [1:0] MUX_PC,
  input  MUX_JALR
);

  wire not_1_out;
  wire [0:0] IR_q_3;
  wire [2:0] multiplexer_6_out;
  wire [6:6] IR_q_5;
  wire [7:0] IR_q_2;
  wire [9:0] IR_q_4;
  wire [11:0] IR_q, multiplexer_3_out;
  wire [31:0] add_1_s, banc_de_registres_1_src1, banc_de_registres_1_src2, bitextender_1_out,
       bitextender_2_out, bitextender_3_out, branch_1_p1, driver_1_out, MAR_q, MDR_q, multiplexer_1_out,
       multiplexer_2_out, multiplexer_4_out, multiplexer_5_out, PC_q, ramsingleportsel_1_d;

  Multiplexer #(.Bits(32)) multiplexer_1 (.sel(MUX_JALR), .in_0(add_1_s), .in_1(driver_1_out), .out(multiplexer_1_out));
  Register #(.Bits(32)) PC (.D(multiplexer_1_out), .C(W_PC), .en(W_PC), .Q(PC_q));
  Add #(.Bits(32)) add_1 (.a(multiplexer_2_out), .b(PC_q), .c_i(1'b0), .s(add_1_s));  // open: c_o
  Multiplexer #(.Selector_Bits(2), .Bits(32)) multiplexer_2 (
    .sel(MUX_PC), .in_0(32'h4), .in_1(bitextender_2_out), .in_2(32'h4), .in_3(bitextender_1_out),
    .out(multiplexer_2_out));
  Register #(.Bits(32)) IR (.D(driver_1_out), .C(W_IR), .en(W_IR), .Q({IR_q_5[6], IR_q_4, IR_q_3[0], IR_q_2, IR_q}));
  assign driver_1_out = G_PC ? PC_q : 32'bz;  // Driver driver_1
  BitExtender #(.inputBits(20), .outputBits(32)) bitextender_1 (
    .in({IR_q_5[6], IR_q_2, IR_q_3[0], IR_q_4}), .out(bitextender_1_out));
  BitExtender #(.inputBits(12), .outputBits(32)) bitextender_2 (
    .in({IR_q_4[4], IR_q[7], IR_q_5[6], IR_q_4[9:5], IR_q[11:8]}), .out(bitextender_2_out));
  Multiplexer #(.Bits(12)) multiplexer_3 (
    .sel(MUX_IM), .in_0({IR_q_5[6], IR_q_4, IR_q_3[0]}), .in_1({IR_q_5[6], IR_q_4[9:4], IR_q[11:7]}),
    .out(multiplexer_3_out));
  Register #(.Bits(32)) MAR (.D(driver_1_out), .C(W_MAR), .en(W_MAR), .Q(MAR_q));
  BitExtender #(.inputBits(12), .outputBits(32)) bitextender_3 (.in(multiplexer_3_out), .out(bitextender_3_out));
  Banc_De_Registres banc_de_registres_1 (
    .Wreg(W_RES), .rd(IR_q[11:7]), .rs1(IR_q_2[7:3]), .rs2({IR_q_4[3:0], IR_q_3[0]}), .res(driver_1_out),
    .src1(banc_de_registres_1_src1), .src2(banc_de_registres_1_src2));  // open: x5, x6, x7
  not not_1 (not_1_out, W_MDR_2);
  RAMSinglePortSel #(.AddrBits(8), .Bits(32)) ramsingleportsel_1 (
    .A(MAR_q[9:2]), .CS(1'b1), .WE(W_MDR_2), .OE(not_1_out), .D(ramsingleportsel_1_d));
  assign driver_1_out = G_RS2 ? banc_de_registres_1_src2 : 32'bz;  // Driver driver_2
  Multiplexer #(.Bits(32)) multiplexer_4 (
    .sel(MUX_MDR), .in_0(ramsingleportsel_1_d), .in_1(driver_1_out), .out(multiplexer_4_out));
  // BRANCH branch_1: pin names not known; wires that end beside it: branch_1_p1, IR_q_2[2:0]
  Multiplexer #(.Bits(32)) multiplexer_5 (
    .sel(MUX_ALU), .in_0(banc_de_registres_1_src2), .in_1(bitextender_3_out), .out(multiplexer_5_out));
  Register #(.Bits(32)) MDR (.D(multiplexer_4_out), .C(W_MDR), .en(W_MDR), .Q(MDR_q));
  Multiplexer #(.Bits(3)) multiplexer_6 (.sel(MUX_FCT3), .in_0(IR_q_2[2:0]), .in_1(3'b000), .out(multiplexer_6_out));
  assign ramsingleportsel_1_d = W_MDR_2 ? MDR_q : 32'bz;  // Driver driver_3
  // UAL__1 ual__1_1: pin names not known; wires that end beside it: SUB, multiplexer_6_out, banc_de_registres_1_src1, multiplexer_5_out, branch_1_p1
  assign driver_1_out = G_MDR ? MDR_q : 32'bz;  // Driver driver_4
  assign driver_1_out = G_ALU ? branch_1_p1 : 32'bz;  // Driver driver_5
endmodule
