// Digital circuit Datapath0.dig as structural Verilog
module Datapath0 (
  input  MUX_ALU,
  input  SUB,
  input  WPC,
  input  G_ALU,
  input  W_MAR,
  input  W_MAR_2,
  input  MUX_MAR,
  input  W_RES,
  input  G_MDR,
  input  G_MDR_2,
  input  W_RI,
  input  G_PC
);

  wire not_1_out;
  wire [31:0] add_1_s, banc_de_registre_1_src1, banc_de_registre_1_src2, bitextender_1_out, driver_1_out,
       MAR_q, MDR_q, multiplexer_1_out, multiplexer_2_out, PC_q, ramsingleportsel_1_d, RI_q, ual_1_s;

  Add #(.Bits(32)) add_1 (.a(32'h4), .b(PC_q), .c_i(1'b0), .s(add_1_s));  // open: c_o
  Register #(.Bits(32)) PC (.D(add_1_s), .C(WPC), .en(WPC), .Q(PC_q));
  assign driver_1_out = G_PC ? PC_q : 32'bz;  // Driver driver_1
  Register #(.Bits(32)) RI (.D(driver_1_out), .C(W_RI), .en(W_RI), .Q(RI_q));
  Register #(.Bits(32)) MAR (.D(driver_1_out), .C(W_MAR), .en(W_MAR), .Q(MAR_q));
  not not_1 (not_1_out, G_MDR_2);
  BitExtender #(.inputBits(7), .outputBits(32)) bitextender_1 (.in(RI_q[31:25]), .out(bitextender_1_out));
  RAMSinglePortSel #(.AddrBits(8), .Bits(32)) ramsingleportsel_1 (
    .A(MAR_q[9:2]), .CS(1'b1), .WE(G_MDR_2), .OE(not_1_out), .D(ramsingleportsel_1_d));
  Banc_de_registre banc_de_registre_1 (
    .CLK(W_RES), .rd(RI_q[11:7]), .rs1(RI_q[19:15]), .rs2(RI_q[24:20]), .Res(driver_1_out),
    .src1(banc_de_registre_1_src1), .src2(banc_de_registre_1_src2));
  Multiplexer #(.Bits(32)) multiplexer_1 (
    .sel(MUX_ALU), .in_0(banc_de_registre_1_src2), .in_1(bitextender_1_out), .out(multiplexer_1_out));
  UAL ual_1 (.Funct3(RI_q[14:12]), .a(banc_de_registre_1_src1), .b(multiplexer_1_out), .Sub(SUB), .S(ual_1_s));
  Multiplexer #(.Bits(32)) multiplexer_2 (
    .sel(MUX_MAR), .in_0(ramsingleportsel_1_d), .in_1(driver_1_out), .out(multiplexer_2_out));
  Register #(.Bits(32)) MDR (.D(multiplexer_2_out), .C(W_MAR_2), .en(W_MAR_2), .Q(MDR_q));
  assign driver_1_out = G_ALU ? ual_1_s : 32'bz;  // Driver driver_2
  assign ramsingleportsel_1_d = G_MDR_2 ? MDR_q : 32'bz;  // Driver driver_3
  assign driver_1_out = G_MDR ? MDR_q : 32'bz;  // Driver driver_4
endmodule
