// Digital circuit Datapath3.dig as structural Verilog
module Datapath3 (
  input  MUX_ALU,
  input  SUB,
  input  WPC,
  input  G_ALU,
  input  W_MAR,
  input  W_MAR_2,
  input  MUX_MAR,
  input  W_RES,
  input  G_MDR,
  input  G_MDR_2,
  input  W_RI,
  input  G_PC,
  input  G_STORE,
  input  MUX_STORE,
  input  [1:0] MUX_PC,
  input  MUX_FUNCT3
);

  wire not_1_out;
  wire [2:0] multiplexer_4_out, RI_q_3;
  wire [3:0] RI_q_5;
  wire [4:0] RI_q_2, RI_q_4;
  wire [11:0] multiplexer_2_out;
  wire [11:4] RI_q_6;
  wire [20:0] RI_q;
  wire [31:0] add_1_s, banc_de_registre_1_src1, banc_de_registre_1_src2, bitextender_1_out,
       bitextender_2_out, bitextender_3_out, driver_1_out, MAR_q, MDR_q, multiplexer_1_out,
       multiplexer_3_out, multiplexer_5_out, PC_q, ramsingleportsel_1_d, ual_1_s;

  Add #(.Bits(32)) add_1 (.a(multiplexer_1_out), .b(PC_q), .c_i(1'b0), .s(add_1_s));  // open: c_o
  Multiplexer #(.Selector_Bits(2), .Bits(32)) multiplexer_1 (
    .sel(MUX_PC), .in_0(32'h4), .in_1(bitextender_1_out), .in_2(32'h4), .in_3(bitextender_2_out),
    .out(multiplexer_1_out));
  BitExtender #(.inputBits(12), .outputBits(32)) bitextender_1 (
    .in({RI_q_6[11], RI_q_2[0], RI_q_6[9:4], RI_q_2[4:1]}), .out(bitextender_1_out));
  Register #(.Bits(32)) PC (.D(add_1_s), .C(WPC), .en(WPC), .Q(PC_q));
  BitExtender #(.inputBits(20), .outputBits(32)) bitextender_2 (
    .in({RI_q_6[11], RI_q_4, RI_q_3, RI_q[20], RI_q_6[9:4], RI_q_5}), .out(bitextender_2_out));
  assign driver_1_out = G_PC ? PC_q : 32'bz;  // Driver driver_1
  Register #(.Bits(32)) RI (
    .D(driver_1_out), .C(W_RI), .en(W_RI),
    .Q({RI_q_6[11], RI_q_6[9:4], RI_q_5, RI_q[20], RI_q_4, RI_q_3, RI_q_2, RI_q[6:0]}));
  Register #(.Bits(32)) MAR (.D(driver_1_out), .C(W_MAR), .en(W_MAR), .Q(MAR_q));
  not not_1 (not_1_out, G_MDR_2);
  BRANCH branch_1 (.RES(ual_1_s), .funct3(RI_q_3));  // open: Taken
  Multiplexer #(.Bits(12)) multiplexer_2 (
    .sel(MUX_STORE), .in_0({RI_q_6[11], RI_q_6[9:4], RI_q_2}),
    .in_1({RI_q_6[11], RI_q_6[9:4], RI_q_5, RI_q[20]}), .out(multiplexer_2_out));
  RAMSinglePortSel #(.AddrBits(8), .Bits(32)) ramsingleportsel_1 (
    .A(MAR_q[9:2]), .CS(1'b1), .WE(G_MDR_2), .OE(not_1_out), .D(ramsingleportsel_1_d));
  Banc_de_registre banc_de_registre_1 (
    .CLK(W_RES), .rd(RI_q_2), .rs1(RI_q_4), .rs2({RI_q_5, RI_q[20]}), .Res(driver_1_out),
    .src1(banc_de_registre_1_src1), .src2(banc_de_registre_1_src2));
  BitExtender #(.inputBits(12), .outputBits(32)) bitextender_3 (.in(multiplexer_2_out), .out(bitextender_3_out));
  Multiplexer #(.Bits(32)) multiplexer_3 (
    .sel(MUX_ALU), .in_0(banc_de_registre_1_src2), .in_1(bitextender_3_out), .out(multiplexer_3_out));
  Multiplexer #(.Bits(3)) multiplexer_4 (.sel(MUX_FUNCT3), .in_0(RI_q_3), .in_1(3'b001), .out(multiplexer_4_out));
  assign driver_1_out = G_STORE ? banc_de_registre_1_src2 : 32'bz;  // Driver driver_2
  Multiplexer #(.Bits(32)) multiplexer_5 (
    .sel(MUX_MAR), .in_0(ramsingleportsel_1_d), .in_1(driver_1_out), .out(multiplexer_5_out));
  UAL ual_1 (.Funct3(multiplexer_4_out), .a(banc_de_registre_1_src1), .b(multiplexer_3_out), .Sub(SUB), .S(ual_1_s));
  Register #(.Bits(32)) MDR (.D(multiplexer_5_out), .C(W_MAR_2), .en(W_MAR_2), .Q(MDR_q));
  assign driver_1_out = G_ALU ? ual_1_s : 32'bz;  // Driver driver_3
  assign ramsingleportsel_1_d = G_MDR_2 ? MDR_q : 32'bz;  // Driver driver_4
  assign driver_1_out = G_MDR ? MDR_q : 32'bz;  // Driver driver_5
endmodule
