// Digital circuit UAL.dig as structural Verilog
module UAL (
  input  [2:0] Funct3,
  input  [31:0] a,
  input  [31:0] b,
  input  Sub,
  output [31:0] S
);

  wire [31:0] add_1_s, and_1_out, bitextender_1_out, or_1_out, xor_1_out, xor_2_out;

  BitExtender #(.inputBits(1), .outputBits(32)) bitextender_1 (.in(Sub), .out(bitextender_1_out));
  assign xor_1_out = bitextender_1_out ^ b;  // XOr xor_1, 32 bits wide
  Add #(.Bits(32)) add_1 (.a(a), .b(xor_1_out), .c_i(Sub), .s(add_1_s));  // open: c_o
  assign xor_2_out = a ^ b;  // XOr xor_2, 32 bits wide
  assign or_1_out = a | b;  // Or or_1, 32 bits wide
  assign and_1_out = a & b;  // And and_1, 32 bits wide
  Multiplexer #(.Selector_Bits(3), .Bits(32)) multiplexer_1 (
    .sel(Funct3), .in_0(add_1_s), .in_1({32{1'b0}}), .in_2({32{1'b0}}), .in_3({32{1'b0}}), .in_4(xor_2_out),
    .in_5({32{1'b0}}), .in_6(or_1_out), .in_7(and_1_out), .out(S));
endmodule
