// Digital circuit compdec.dig as structural Verilog
module compdec (
  input  w,
  input  reset,
  input  inc,
  output s0,
  output s1,
  output s2
);

  wire and_1_out, and_2_out, and_3_out, and_4_out, and_5_out, and_6_out, and_7_out, and_8_out, and_9_out,
       d_ff_1_nq, d_ff_2_nq, d_ff_3_nq, multiplexer_1_out, multiplexer_2_out, multiplexer_3_out, not_1_out,
       or_1_out, or_2_out, or_3_out, or_4_out, xor_1_out;

  or or_1 (or_1_out, or_2_out, and_1_out);
  and and_1 (and_1_out, and_2_out, d_ff_2_nq);
  or or_2 (or_2_out, and_3_out, and_4_out);
  and and_2 (and_2_out, d_ff_1_nq, d_ff_3_nq);
  and and_3 (and_3_out, s2, xor_1_out);
  or or_3 (or_3_out, and_6_out, and_5_out);
  and and_4 (and_4_out, s2, and_8_out);
  D_FF d_ff_1 (.D(multiplexer_1_out), .C(w), .Q(s2), .nQ(d_ff_1_nq));
  and and_5 (and_5_out, s2, or_4_out);
  and and_6 (and_6_out, d_ff_1_nq, and_7_out);
  Multiplexer #(.Selector_Bits(2)) multiplexer_1 (
    .sel({reset, inc}), .in_0(or_1_out), .in_1(or_3_out), .in_2(1'b0), .in_3(1'b0), .out(multiplexer_1_out));
  or or_4 (or_4_out, xor_1_out, and_9_out);
  and and_7 (and_7_out, s1, s0);
  and and_8 (and_8_out, s1, s0);
  not not_1 (not_1_out, xor_1_out);
  D_FF d_ff_2 (.D(multiplexer_2_out), .C(w), .Q(s1), .nQ(d_ff_2_nq));
  and and_9 (and_9_out, s1, d_ff_3_nq);
  Multiplexer #(.Selector_Bits(2)) multiplexer_2 (
    .sel({reset, inc}), .in_0(not_1_out), .in_1(xor_1_out), .in_2(1'b0), .in_3(1'b0), .out(multiplexer_2_out));
  xor xor_1 (xor_1_out, s1, s0);
  D_FF d_ff_3 (.D(multiplexer_3_out), .C(w), .Q(s0), .nQ(d_ff_3_nq));
  Multiplexer #(.Selector_Bits(2)) multiplexer_3 (
    .sel({reset, inc}), .in_0(d_ff_3_nq), .in_1(d_ff_3_nq), .in_2(1'b0), .in_3(1'b0), .out(multiplexer_3_out));
endmodule
